// Logisim project ETF-evolution.circ as structural Verilog: 88 circuits, main circuit REG1_LD
module ADD1 (
  input  Cin,
  input  A,
  input  B,
  output F,
  output Cout
);

  Adder #(.width(1)) adder_1 (.a(A), .b(B), .out(F), .cin(Cin), .cout(Cout));
endmodule

module ADD8 (
  input  C0,
  input  [7:0] A,
  input  [7:0] B,
  output [7:0] F,
  output C8
);

  Adder adder_1 (.a(A), .b(B), .out(F), .cin(C0), .cout(C8));
endmodule

module ADD9 (
  input  C0,
  input  [8:0] A,
  input  [8:0] B,
  output [8:0] F,
  output C9
);

  Adder #(.width(9)) adder_1 (.a(A), .b(B), .out(F), .cin(C0), .cout(C9));
endmodule

module ADD16 (
  input  C0,
  input  [15:0] A,
  input  [15:0] B,
  output [15:0] F,
  output C16
);

  Adder #(.width(16)) adder_1 (.a(A), .b(B), .out(F), .cin(C0), .cout(C16));
endmodule

module CD4 (
  input  En,
  input  C3,
  input  C2,
  input  C1,
  input  C0,
  output Z1,
  output Z0,
  output W
);

  wire or_1_out, or_2_out, or_3_out;

  Pull_Resistor #(.pull(1)) pull_resistor_1 (.node(En));
  or or_1 (or_1_out, C3, C2, C1, C0);
  or or_2 (or_2_out, C3, C2);
  or or_3 (or_3_out, C3, C1);
  and and_1 (Z1, En, or_2_out);
  and and_2 (Z0, En, or_3_out);
  and and_3 (W, En, or_1_out);

  // Notes on the sheet:
  //   uezti za podrazumevanu vrednost logičku jedinicu
  //   Ako En nije priključen (stanje visoke impednase - HiZ),
endmodule

module CD8 (
  input  En,
  input  C7,
  input  C6,
  input  C5,
  input  C4,
  input  C3,
  input  C2,
  input  C1,
  input  C0,
  output Z2,
  output Z1,
  output Z0,
  output W
);

  wire or_1_out, or_2_out, or_3_out, or_4_out;

  Pull_Resistor #(.pull(1)) pull_resistor_1 (.node(En));
  or or_1 (or_1_out, C7, C6, C5, C4, C3, C2, C1, C0);
  or or_2 (or_2_out, C7, C6, C5, C4);
  or or_3 (or_3_out, C7, C6, C3, C2);
  or or_4 (or_4_out, C7, C5, C3, C1);
  and and_1 (Z2, En, or_2_out);
  and and_2 (Z1, En, or_3_out);
  and and_3 (Z0, En, or_4_out);
  and and_4 (W, En, or_1_out);

  // Notes on the sheet:
  //   uezti za podrazumevanu vrednost logičku jedinicu
  //   Ako En nije priključen (stanje visoke impednase - HiZ),
endmodule

module DC1_2 (
  input  En,
  input  X0,
  output D0,
  output D1
);

  wire not_1_out;

  Pull_Resistor #(.pull(1)) pull_resistor_1 (.node(En));
  not not_1 (not_1_out, X0);
  and and_1 (D0, En, not_1_out);
  and and_2 (D1, En, X0);

  // Notes on the sheet:
  //   Ako En nije priključen (stanje visoke impednase - HiZ),
  //   uezti za podrazumevanu vrednost logičku jedinicu
endmodule

module DC2_4 (
  input  En,
  input  [1:0] X1_0_c7335de0,
  output D0,
  output D1,
  output D2,
  output D3
);

  wire dc1_2_1_d0, dc1_2_1_d1;

  Pull_Resistor #(.pull(1)) pull_resistor_1 (.node(En));
  DC1_2 dc1_2_1 (.D0(dc1_2_1_d0), .D1(dc1_2_1_d1), .X0(X1_0_c7335de0[1]), .En(En));
  DC1_2 dc1_2_2 (.D0(D0), .D1(D1), .X0(X1_0_c7335de0[0]), .En(dc1_2_1_d0));
  DC1_2 dc1_2_3 (.D0(D2), .D1(D3), .X0(X1_0_c7335de0[0]), .En(dc1_2_1_d1));

  // Notes on the sheet:
  //   Ako En nije priključen (stanje visoke impednase - HiZ),
  //   uezti za podrazumevanu vrednost logičku jedinicu
endmodule

module DC3_8 (
  input  En,
  input  [2:0] X2_0_5144ffce,
  output D0,
  output D1,
  output D2,
  output D3,
  output D4,
  output D5,
  output D6,
  output D7
);

  wire dc1_2_1_d0, dc1_2_1_d1;

  Pull_Resistor #(.pull(1)) pull_resistor_1 (.node(En));
  DC1_2 dc1_2_1 (.D0(dc1_2_1_d0), .D1(dc1_2_1_d1), .X0(X2_0_5144ffce[2]), .En(En));
  DC2_4 dc2_4_1 (.D0(D0), .D1(D1), .D2(D2), .D3(D3), .X1_0_c7335de0(X2_0_5144ffce[1:0]), .En(dc1_2_1_d0));
  DC2_4 dc2_4_2 (.D0(D4), .D1(D5), .D2(D6), .D3(D7), .X1_0_c7335de0(X2_0_5144ffce[1:0]), .En(dc1_2_1_d1));

  // Notes on the sheet:
  //   Ako En nije priključen (stanje visoke impednase - HiZ),
  //   uezti za podrazumevanu vrednost logičku jedinicu
endmodule

module DC4_16 (
  input  En,
  input  [3:0] X3_0_7fef0577,
  output D0,
  output D1,
  output D2,
  output D3,
  output D4,
  output D5,
  output D6,
  output D7,
  output D8,
  output D9,
  output D10,
  output D11,
  output D12,
  output D13,
  output D14,
  output D15
);

  wire dc1_2_1_d0, dc1_2_1_d1;

  Pull_Resistor #(.pull(1)) pull_resistor_1 (.node(En));
  DC1_2 dc1_2_1 (.D0(dc1_2_1_d0), .D1(dc1_2_1_d1), .X0(X3_0_7fef0577[3]), .En(En));
  DC3_8 dc3_8_1 (
    .D0(D0), .D1(D1), .D2(D2), .D3(D3), .D4(D4), .D5(D5), .D6(D6), .D7(D7),
    .X2_0_5144ffce(X3_0_7fef0577[2:0]), .En(dc1_2_1_d0));
  DC3_8 dc3_8_2 (
    .D0(D8), .D1(D9), .D2(D10), .D3(D11), .D4(D12), .D5(D13), .D6(D14), .D7(D15),
    .X2_0_5144ffce(X3_0_7fef0577[2:0]), .En(dc1_2_1_d1));

  // Notes on the sheet:
  //   Ako En nije priključen (stanje visoke impednase - HiZ),
  //   uezti za podrazumevanu vrednost logičku jedinicu
endmodule

module REG1 (
  input  CL,
  input  LD,
  input  I,
  input  SL,
  input  IL,
  input  SR,
  input  IR,
  input  INC,
  input  DEC,
  input  CLK,
  output Cout,
  output Eout,
  output A
);

  wire and_1_out, and_2_out, and_3_out, and_4_out, and_5_out, and_6_out, and_7_out, and_8_out, and_9_out,
       and_10_out, or_1_out, or_2_out, rsff_1_notq;

  Pull_Resistor pull_resistor_1 (.node(CL));
  Pull_Resistor pull_resistor_2 (.node(LD));
  Pull_Resistor pull_resistor_3 (.node(SL));
  Pull_Resistor pull_resistor_4 (.node(SR));
  Pull_Resistor pull_resistor_5 (.node(INC));
  Pull_Resistor pull_resistor_6 (.node(DEC));
  and and_1 (and_1_out, LD, ~I);  // AND_Gate
  and and_2 (and_2_out, LD, I);
  and and_3 (and_3_out, SL, ~IL);  // AND_Gate
  and and_4 (and_4_out, SL, IL);
  and and_5 (and_5_out, SR, ~IR);  // AND_Gate
  and and_6 (and_6_out, SR, IR);
  and and_7 (and_7_out, A, INC);
  and and_8 (and_8_out, ~A, INC);  // AND_Gate
  and and_9 (and_9_out, A, DEC);
  and and_10 (and_10_out, ~A, DEC);  // AND_Gate
  or or_1 (or_1_out, and_10_out, and_8_out, and_6_out, and_4_out, and_2_out);
  or or_2 (or_2_out, and_9_out, and_7_out, and_5_out, and_3_out, and_1_out, CL);
  RSFF rsff_1 (.Q(A), .notQ(rsff_1_notq), .S(or_1_out), .R(or_2_out), .CLK(CLK));  // open: Sd, Rd
  and and_11 (Cout, A, INC);
  and and_12 (Eout, ~A, DEC);  // AND_Gate

  // Notes on the sheet:
  //   Ako neka operacija (CL, LD, SL, SR, INC, DEC) nije priključen (stanje visoke impednase - HiZ),
  //   uezti za podrazumevanu vrednost logičku nulu
endmodule

module REG8 (
  input  CL,
  input  LD,
  input  [7:0] A,
  input  SL,
  input  IL,
  input  SR,
  input  IR,
  input  DEC,
  input  INC,
  input  CLK,
  output Cout,
  output Eout,
  output [7:0] I
);

  wire reg1_2_cout, reg1_2_eout, reg1_3_cout, reg1_3_eout, reg1_4_cout, reg1_4_eout, reg1_5_cout,
       reg1_5_eout, reg1_6_cout, reg1_6_eout, reg1_7_cout, reg1_7_eout, reg1_8_cout, reg1_8_eout;

  REG1 reg1_1 (
    .Cout(Cout), .Eout(Eout), .A(I[7]), .CL(CL), .LD(LD), .I(A[7]), .SL(SL), .IL(I[6]), .SR(SR), .IR(IR),
    .INC(reg1_2_cout), .DEC(reg1_2_eout), .CLK(CLK));
  REG1 reg1_2 (
    .Cout(reg1_2_cout), .Eout(reg1_2_eout), .A(I[6]), .CL(CL), .LD(LD), .I(A[6]), .SL(SL), .IL(I[5]),
    .SR(SR), .IR(I[7]), .INC(reg1_3_cout), .DEC(reg1_3_eout), .CLK(CLK));
  REG1 reg1_3 (
    .Cout(reg1_3_cout), .Eout(reg1_3_eout), .A(I[5]), .CL(CL), .LD(LD), .I(A[5]), .SL(SL), .IL(I[4]),
    .SR(SR), .IR(I[6]), .INC(reg1_4_cout), .DEC(reg1_4_eout), .CLK(CLK));
  REG1 reg1_4 (
    .Cout(reg1_4_cout), .Eout(reg1_4_eout), .A(I[4]), .CL(CL), .LD(LD), .I(A[4]), .SL(SL), .IL(I[3]),
    .SR(SR), .IR(I[5]), .INC(reg1_5_cout), .DEC(reg1_5_eout), .CLK(CLK));
  REG1 reg1_5 (
    .Cout(reg1_5_cout), .Eout(reg1_5_eout), .A(I[3]), .CL(CL), .LD(LD), .I(A[3]), .SL(SL), .IL(I[2]),
    .SR(SR), .IR(I[4]), .INC(reg1_6_cout), .DEC(reg1_6_eout), .CLK(CLK));
  REG1 reg1_6 (
    .Cout(reg1_6_cout), .Eout(reg1_6_eout), .A(I[2]), .CL(CL), .LD(LD), .I(A[2]), .SL(SL), .IL(I[1]),
    .SR(SR), .IR(I[3]), .INC(reg1_7_cout), .DEC(reg1_7_eout), .CLK(CLK));
  REG1 reg1_7 (
    .Cout(reg1_7_cout), .Eout(reg1_7_eout), .A(I[1]), .CL(CL), .LD(LD), .I(A[1]), .SL(SL), .IL(I[0]),
    .SR(SR), .IR(I[2]), .INC(reg1_8_cout), .DEC(reg1_8_eout), .CLK(CLK));
  REG1 reg1_8 (
    .Cout(reg1_8_cout), .Eout(reg1_8_eout), .A(I[0]), .CL(CL), .LD(LD), .I(A[0]), .SL(SL), .IL(IL), .SR(SR),
    .IR(I[1]), .INC(INC), .DEC(DEC), .CLK(CLK));

  // Notes on the sheet:
  //   7..0
  //   7..0
endmodule

module REG16 (
  input  CL,
  input  LD,
  input  [15:0] A,
  input  SL,
  input  IL,
  input  SR,
  input  IR,
  input  DEC,
  input  INC,
  input  CLK,
  output Cout,
  output Eout,
  output [15:0] I
);

  wire reg8_2_cout, reg8_2_eout;

  REG8 reg8_1 (
    .I(I[15:8]), .Cout(Cout), .Eout(Eout), .CL(CL), .LD(LD), .SL(SL), .IL(I[7]), .SR(SR), .IR(IR),
    .DEC(reg8_2_eout), .INC(reg8_2_cout), .CLK(CLK), .A(A[15:8]));
  REG8 reg8_2 (
    .I(I[7:0]), .Cout(reg8_2_cout), .Eout(reg8_2_eout), .CL(CL), .LD(LD), .SL(SL), .IL(IL), .SR(SR),
    .IR(I[8]), .DEC(DEC), .INC(INC), .CLK(CLK), .A(A[7:0]));

  // Notes on the sheet:
  //   15..0
  //   15..0
endmodule

module REG1_DEC_LD (
  input  I0,
  input  LD,
  input  DEC,
  input  CLK,
  output A0
);

  REG1m_DEC_LD reg1m_dec_ld_1 (.Ai(A0), .DEC(DEC), .Ei(DEC), .CLK(CLK), .Ii(I0), .LD(LD));  // open: Eout
endmodule

module REG2_DEC_LD (
  input  [1:0] I1_0_431d2720,
  input  LD,
  input  DEC,
  input  CLK,
  output [1:0] A1_0_e4900909
);

  REG2m_DEC_LD reg2m_dec_ld_1 (
    .A1_0_e4900909(A1_0_e4900909), .LD(LD), .Ein(DEC), .DEC(DEC), .CLK(CLK), .I1_0_431d2720(I1_0_431d2720));  // open: Eout
endmodule

module REG3_DEC_LD (
  input  [2:0] I2_0_589fad62,
  input  LD,
  input  DEC,
  input  CLK,
  output [2:0] A2_0_8a36edda
);

  wire reg1m_dec_ld_2_eout, reg1m_dec_ld_3_eout;

  REG1m_DEC_LD reg1m_dec_ld_1 (
    .Ai(A2_0_8a36edda[2]), .DEC(DEC), .Ei(reg1m_dec_ld_2_eout), .CLK(CLK), .Ii(I2_0_589fad62[2]), .LD(LD));  // open: Eout
  REG1m_DEC_LD reg1m_dec_ld_2 (
    .Ai(A2_0_8a36edda[1]), .Eout(reg1m_dec_ld_2_eout), .DEC(DEC), .Ei(reg1m_dec_ld_3_eout), .CLK(CLK),
    .Ii(I2_0_589fad62[1]), .LD(LD));
  REG1m_DEC_LD reg1m_dec_ld_3 (
    .Ai(A2_0_8a36edda[0]), .Eout(reg1m_dec_ld_3_eout), .DEC(DEC), .Ei(DEC), .CLK(CLK), .Ii(I2_0_589fad62[0]),
    .LD(LD));
endmodule

module REG1_LD (
  input  Ii,
  input  LD,
  input  CLK,
  output Ai
);

  wire and_1_out, and_2_out, or_1_out;

  and and_1 (and_1_out, Ii, LD);
  and and_2 (and_2_out, ~LD, Ai);  // AND_Gate
  or or_1 (or_1_out, and_1_out, and_2_out);
  DFF dff_1 (.Q(Ai), .D(or_1_out), .CLK(CLK));  // open: notQ, Sd, Rd
endmodule

module REG2_LD (
  input  [1:0] I1_0_431d2720,
  input  LD,
  input  CLK,
  output [1:0] A1_0_e4900909
);

  REG1_LD reg1_ld_1 (.Ai(A1_0_e4900909[1]), .CLK(CLK), .Ii(I1_0_431d2720[1]), .LD(LD));
  REG1_LD reg1_ld_2 (.Ai(A1_0_e4900909[0]), .CLK(CLK), .Ii(I1_0_431d2720[0]), .LD(LD));
endmodule

module REG3_LD (
  input  [2:0] I2_0_589fad62,
  input  LD,
  input  CLK,
  output [2:0] A2_0_8a36edda
);

  REG1_LD reg1_ld_1 (.Ai(A2_0_8a36edda[2]), .CLK(CLK), .Ii(I2_0_589fad62[2]), .LD(LD));
  REG1_LD reg1_ld_2 (.Ai(A2_0_8a36edda[1]), .CLK(CLK), .Ii(I2_0_589fad62[1]), .LD(LD));
  REG1_LD reg1_ld_3 (.Ai(A2_0_8a36edda[0]), .CLK(CLK), .Ii(I2_0_589fad62[0]), .LD(LD));
endmodule

module REG4_LD (
  input  [3:0] I3_0_530b42ff,
  input  LD,
  input  CLK,
  output [3:0] A3_0_6aaf74d5
);

  REG2_LD reg2_ld_1 (.A1_0_e4900909(A3_0_6aaf74d5[3:2]), .LD(LD), .CLK(CLK), .I1_0_431d2720(I3_0_530b42ff[3:2]));
  REG2_LD reg2_ld_2 (.A1_0_e4900909(A3_0_6aaf74d5[1:0]), .LD(LD), .CLK(CLK), .I1_0_431d2720(I3_0_530b42ff[1:0]));
endmodule

module REG8_LD (
  input  [7:0] I7_0_76b06db5,
  input  LD,
  input  CLK,
  output [7:0] A7_0_536de17e
);

  REG4_LD reg4_ld_1 (.A3_0_6aaf74d5(A7_0_536de17e[7:4]), .LD(LD), .CLK(CLK), .I3_0_530b42ff(I7_0_76b06db5[7:4]));
  REG4_LD reg4_ld_2 (.A3_0_6aaf74d5(A7_0_536de17e[3:0]), .LD(LD), .CLK(CLK), .I3_0_530b42ff(I7_0_76b06db5[3:0]));
endmodule

module REG10_LD (
  input  [9:0] I9_0_3e8b5057,
  input  LD,
  input  CLK,
  output [9:0] A9_0_5e2553cd
);

  REG2_LD reg2_ld_1 (.A1_0_e4900909(A9_0_5e2553cd[9:8]), .LD(LD), .CLK(CLK), .I1_0_431d2720(I9_0_3e8b5057[9:8]));
  REG8_LD reg8_ld_1 (.A7_0_536de17e(A9_0_5e2553cd[7:0]), .LD(LD), .CLK(CLK), .I7_0_76b06db5(I9_0_3e8b5057[7:0]));
endmodule

module REG16_LD (
  input  [15:0] I15_0_dbedc2e3,
  input  LD,
  input  CLK,
  output [15:0] A15_0_fec680c4
);

  REG8_LD reg8_ld_1 (.A7_0_536de17e(A15_0_fec680c4[15:8]), .LD(LD), .CLK(CLK), .I7_0_76b06db5(I15_0_dbedc2e3[15:8]));
  REG8_LD reg8_ld_2 (.A7_0_536de17e(A15_0_fec680c4[7:0]), .LD(LD), .CLK(CLK), .I7_0_76b06db5(I15_0_dbedc2e3[7:0]));
endmodule

module REG1_LD_SR (
  input  Ii,
  input  LD,
  input  IR,
  input  SR,
  input  CLK,
  output Ai
);

  wire and_1_out, and_2_out, and_3_out, or_1_out;

  and and_1 (and_1_out, IR, SR);
  and and_2 (and_2_out, Ii, LD);
  and and_3 (and_3_out, ~LD, ~SR, Ai);  // AND_Gate
  or or_1 (or_1_out, and_2_out, and_1_out, and_3_out);
  DFF dff_1 (.Q(Ai), .D(or_1_out), .CLK(CLK));  // open: notQ, Sd, Rd
endmodule

module REG2_LD_SR (
  input  [1:0] I1_0_431d2720,
  input  LD,
  input  IR,
  input  SR,
  input  CLK,
  output [1:0] A1_0_e4900909
);

  REG1_LD_SR reg1_ld_sr_1 (.Ai(A1_0_e4900909[1]), .IR(IR), .SR(SR), .CLK(CLK), .Ii(I1_0_431d2720[1]), .LD(LD));
  REG1_LD_SR reg1_ld_sr_2 (
    .Ai(A1_0_e4900909[0]), .IR(A1_0_e4900909[1]), .SR(SR), .CLK(CLK), .Ii(I1_0_431d2720[0]), .LD(LD));
endmodule

module REG3_LD_SR (
  input  [2:0] I2_0_589fad62,
  input  LD,
  input  IR,
  input  SR,
  input  CLK,
  output [2:0] A2_0_8a36edda
);

  REG1_LD_SR reg1_ld_sr_1 (.Ai(A2_0_8a36edda[2]), .IR(IR), .SR(SR), .CLK(CLK), .Ii(I2_0_589fad62[2]), .LD(LD));
  REG2_LD_SR reg2_ld_sr_1 (
    .A1_0_e4900909(A2_0_8a36edda[1:0]), .LD(LD), .IR(A2_0_8a36edda[2]), .SR(SR), .CLK(CLK),
    .I1_0_431d2720(I2_0_589fad62[1:0]));
endmodule

module REG4_LD_SR (
  input  [3:0] I3_0_530b42ff,
  input  LD,
  input  IR,
  input  SR,
  input  CLK,
  output [3:0] A3_0_6aaf74d5
);

  REG2_LD_SR reg2_ld_sr_1 (
    .A1_0_e4900909(A3_0_6aaf74d5[3:2]), .LD(LD), .IR(IR), .SR(SR), .CLK(CLK),
    .I1_0_431d2720(I3_0_530b42ff[3:2]));
  REG2_LD_SR reg2_ld_sr_2 (
    .A1_0_e4900909(A3_0_6aaf74d5[1:0]), .LD(LD), .IR(A3_0_6aaf74d5[2]), .SR(SR), .CLK(CLK),
    .I1_0_431d2720(I3_0_530b42ff[1:0]));
endmodule

module REG8_LD_SR (
  input  [7:0] I7_0_76b06db5,
  input  LD,
  input  IR,
  input  SR,
  input  CLK,
  output [7:0] A7_0_536de17e
);

  REG4_LD_SR reg4_ld_sr_1 (
    .A3_0_6aaf74d5(A7_0_536de17e[7:4]), .LD(LD), .IR(IR), .SR(SR), .CLK(CLK),
    .I3_0_530b42ff(I7_0_76b06db5[7:4]));
  REG4_LD_SR reg4_ld_sr_2 (
    .A3_0_6aaf74d5(A7_0_536de17e[3:0]), .LD(LD), .IR(A7_0_536de17e[4]), .SR(SR), .CLK(CLK),
    .I3_0_530b42ff(I7_0_76b06db5[3:0]));
endmodule

module REG1_LD_SL_SR (
  input  Ii,
  input  LD,
  input  IR,
  input  SR,
  input  IL,
  input  SL,
  input  CLK,
  output Ai
);

  wire and_1_out, and_2_out, and_3_out, and_4_out, or_1_out;

  and and_1 (and_1_out, Ii, LD);
  and and_2 (and_2_out, IR, SR);
  and and_3 (and_3_out, IL, SL);
  and and_4 (and_4_out, ~LD, ~SR, ~SL, Ai);  // AND_Gate
  or or_1 (or_1_out, and_1_out, and_2_out, and_3_out, and_4_out);
  DFF dff_1 (.Q(Ai), .D(or_1_out), .CLK(CLK));  // open: notQ, Sd, Rd
endmodule

module REG2_LD_SL_SR (
  input  [1:0] I1_0_431d2720,
  input  LD,
  input  IR,
  input  SR,
  input  IL,
  input  SL,
  input  CLK,
  output [1:0] A1_0_e4900909
);

  REG1_LD_SL_SR reg1_ld_sl_sr_1 (
    .Ai(A1_0_e4900909[1]), .IR(IR), .SR(SR), .IL(A1_0_e4900909[0]), .SL(SL), .CLK(CLK),
    .Ii(I1_0_431d2720[1]), .LD(LD));
  REG1_LD_SL_SR reg1_ld_sl_sr_2 (
    .Ai(A1_0_e4900909[0]), .IR(A1_0_e4900909[1]), .SR(SR), .IL(IL), .SL(SL), .CLK(CLK),
    .Ii(I1_0_431d2720[0]), .LD(LD));
endmodule

module REG3_LD_SL_SR (
  input  [2:0] I2_0_589fad62,
  input  LD,
  input  IR,
  input  SR,
  input  IL,
  input  SL,
  input  CLK,
  output [2:0] A2_0_8a36edda
);

  REG1_LD_SL_SR reg1_ld_sl_sr_1 (
    .Ai(A2_0_8a36edda[2]), .IR(IR), .SR(SR), .IL(A2_0_8a36edda[1]), .SL(SL), .CLK(CLK),
    .Ii(I2_0_589fad62[2]), .LD(LD));
  REG2_LD_SL_SR reg2_ld_sl_sr_1 (
    .A1_0_e4900909(A2_0_8a36edda[1:0]), .IR(A2_0_8a36edda[2]), .SR(SR), .IL(IL), .SL(SL), .CLK(CLK),
    .I1_0_431d2720(I2_0_589fad62[1:0]), .LD(LD));
endmodule

module REG4_LD_SL_SR (
  input  [3:0] I3_0_530b42ff,
  input  LD,
  input  IR,
  input  SR,
  input  IL,
  input  SL,
  input  CLK,
  output [3:0] A3_0_6aaf74d5
);

  REG2_LD_SL_SR reg2_ld_sl_sr_1 (
    .A1_0_e4900909(A3_0_6aaf74d5[3:2]), .IR(IR), .SR(SR), .IL(A3_0_6aaf74d5[1]), .SL(SL), .CLK(CLK),
    .I1_0_431d2720(I3_0_530b42ff[3:2]), .LD(LD));
  REG2_LD_SL_SR reg2_ld_sl_sr_2 (
    .A1_0_e4900909(A3_0_6aaf74d5[1:0]), .IR(A3_0_6aaf74d5[2]), .SR(SR), .IL(IL), .SL(SL), .CLK(CLK),
    .I1_0_431d2720(I3_0_530b42ff[1:0]), .LD(LD));
endmodule

module REG8_LD_SL_SR (
  input  [7:0] I7_0_76b06db5,
  input  LD,
  input  IR,
  input  SR,
  input  IL,
  input  SL,
  input  CLK,
  output [7:0] A7_0_536de17e
);

  REG4_LD_SL_SR reg4_ld_sl_sr_1 (
    .A3_0_6aaf74d5(A7_0_536de17e[7:4]), .IR(IR), .SR(SR), .IL(A7_0_536de17e[3]), .SL(SL), .CLK(CLK),
    .I3_0_530b42ff(I7_0_76b06db5[7:4]), .LD(LD));
  REG4_LD_SL_SR reg4_ld_sl_sr_2 (
    .A3_0_6aaf74d5(A7_0_536de17e[3:0]), .IR(A7_0_536de17e[4]), .SR(SR), .IL(IL), .SL(SL), .CLK(CLK),
    .I3_0_530b42ff(I7_0_76b06db5[3:0]), .LD(LD));
endmodule

module REG1_CL_LD (
  input  Ii,
  input  LD,
  input  CL,
  input  CLK,
  output Ai
);

  wire and_1_out, and_2_out, or_1_out;

  and and_1 (and_1_out, Ii, LD);
  and and_2 (and_2_out, ~LD, ~CL, Ai);  // AND_Gate
  or or_1 (or_1_out, and_1_out, and_2_out);
  DFF dff_1 (.Q(Ai), .D(or_1_out), .CLK(CLK));  // open: notQ, Sd, Rd
endmodule

module REG8_CL_LD (
  input  [7:0] _7__0,
  input  LD,
  input  CL,
  input  CLK,
  output [7:0] _7__0_2
);

  REG1_CL_LD reg1_cl_ld_1 (.Ai(_7__0_2[7]), .CL(CL), .CLK(CLK), .Ii(_7__0[7]), .LD(LD));
  REG1_CL_LD reg1_cl_ld_2 (.Ai(_7__0_2[6]), .CL(CL), .CLK(CLK), .Ii(_7__0[6]), .LD(LD));
  REG1_CL_LD reg1_cl_ld_3 (.Ai(_7__0_2[5]), .CL(CL), .CLK(CLK), .Ii(_7__0[5]), .LD(LD));
  REG1_CL_LD reg1_cl_ld_4 (.Ai(_7__0_2[4]), .CL(CL), .CLK(CLK), .Ii(_7__0[4]), .LD(LD));
  REG1_CL_LD reg1_cl_ld_5 (.Ai(_7__0_2[3]), .CL(CL), .CLK(CLK), .Ii(_7__0[3]), .LD(LD));
  REG1_CL_LD reg1_cl_ld_6 (.Ai(_7__0_2[2]), .CL(CL), .CLK(CLK), .Ii(_7__0[2]), .LD(LD));
  REG1_CL_LD reg1_cl_ld_7 (.Ai(_7__0_2[1]), .CL(CL), .CLK(CLK), .Ii(_7__0[1]), .LD(LD));
  REG1_CL_LD reg1_cl_ld_8 (.Ai(_7__0_2[0]), .CL(CL), .CLK(CLK), .Ii(_7__0[0]), .LD(LD));

  // Notes on the sheet:
  //   I
  //   A
endmodule

module REG16_CL_LD (
  input  [15:0] _15__0,
  input  LD,
  input  CL,
  input  CLK,
  output [15:0] out_5
);

  REG8_CL_LD reg8_cl_ld_1 (._7__0_2(out_5[15:8]), .LD(LD), .CL(CL), .CLK(CLK), ._7__0(_15__0[15:8]));
  REG8_CL_LD reg8_cl_ld_2 (._7__0_2(out_5[7:0]), .LD(LD), .CL(CL), .CLK(CLK), ._7__0(_15__0[7:0]));

  // Notes on the sheet:
  //   I
  //   A
  //   15..0
endmodule

module REG1_CL_INC (
  input  CL,
  input  INC,
  input  CLK,
  output A0
);

  REG1m_CL_INC reg1m_cl_inc_1 (.Ai(A0), .Ci(INC), .CLK(CLK), .CL(CL), .INC(INC));  // open: Cout
endmodule

module REG2_CL_INC (
  input  CL,
  input  INC,
  input  CLK,
  output [1:0] A1_0_e4900909
);

  REG2m_CL_INC reg2m_cl_inc_1 (.A1_0_e4900909(A1_0_e4900909), .CL(CL), .Cin(INC), .INC(INC), .CLK(CLK));  // open: Cout
endmodule

module REG3_CL_INC (
  input  CL,
  input  INC,
  input  CLK,
  output [2:0] A2_0_8a36edda
);

  wire reg1m_cl_inc_2_cout, reg1m_cl_inc_3_cout;

  REG1m_CL_INC reg1m_cl_inc_1 (
    .Ai(A2_0_8a36edda[2]), .Ci(reg1m_cl_inc_2_cout), .CLK(CLK), .CL(CL), .INC(INC));  // open: Cout
  REG1m_CL_INC reg1m_cl_inc_2 (
    .Cout(reg1m_cl_inc_2_cout), .Ai(A2_0_8a36edda[1]), .Ci(reg1m_cl_inc_3_cout), .CLK(CLK), .CL(CL), .INC(INC));
  REG1m_CL_INC reg1m_cl_inc_3 (
    .Cout(reg1m_cl_inc_3_cout), .Ai(A2_0_8a36edda[0]), .Ci(INC), .CLK(CLK), .CL(CL), .INC(INC));
endmodule

module REG4_CL_INC (
  input  CL,
  input  INC,
  input  CLK,
  output [3:0] A3_0_6aaf74d5
);

  wire reg2m_cl_inc_2_cout;

  REG2m_CL_INC reg2m_cl_inc_1 (
    .A1_0_e4900909(A3_0_6aaf74d5[3:2]), .CL(CL), .Cin(reg2m_cl_inc_2_cout), .INC(INC), .CLK(CLK));  // open: Cout
  REG2m_CL_INC reg2m_cl_inc_2 (
    .Cout(reg2m_cl_inc_2_cout), .A1_0_e4900909(A3_0_6aaf74d5[1:0]), .CL(CL), .Cin(INC), .INC(INC), .CLK(CLK));
endmodule

module REG5_CL_INC (
  input  CL,
  input  INC,
  input  CLK,
  output [4:0] A4_0_c0bc1768
);

  wire reg4m_cl_inc_1_cout;

  REG1m_CL_INC reg1m_cl_inc_1 (
    .Ai(A4_0_c0bc1768[4]), .Ci(reg4m_cl_inc_1_cout), .CLK(CLK), .CL(CL), .INC(INC));  // open: Cout
  REG4m_CL_INC reg4m_cl_inc_1 (
    .Cout(reg4m_cl_inc_1_cout), .A3_0_6aaf74d5(A4_0_c0bc1768[3:0]), .CL(CL), .Cin(INC), .INC(INC), .CLK(CLK));
endmodule

module REG1_CL_INC_LD (
  input  I0,
  input  LD,
  input  CL,
  input  INC,
  input  CLK,
  output A0
);

  REG1m_CL_INC_LD reg1m_cl_inc_ld_1 (.Ai(A0), .CL(CL), .INC(INC), .Ci(INC), .CLK(CLK), .Ii(I0), .LD(LD));  // open: Cout
endmodule

module REG2_CL_INC_LD (
  input  [1:0] I1_0_431d2720,
  input  LD,
  input  CL,
  input  INC,
  input  CLK,
  output [1:0] A1_0_e4900909
);

  REG2m_CL_INC_LD reg2m_cl_inc_ld_1 (
    .A1_0_e4900909(A1_0_e4900909), .LD(LD), .CL(CL), .Cin(INC), .INC(INC), .CLK(CLK),
    .I1_0_431d2720(I1_0_431d2720));  // open: Cout
endmodule

module REG3_CL_INC_LD (
  input  [2:0] I2_0_589fad62,
  input  LD,
  input  CL,
  input  INC,
  input  CLK,
  output [2:0] A2_0_8a36edda
);

  wire reg1m_cl_inc_ld_2_cout, reg1m_cl_inc_ld_3_cout;

  REG1m_CL_INC_LD reg1m_cl_inc_ld_1 (
    .Ai(A2_0_8a36edda[2]), .CL(CL), .INC(INC), .Ci(reg1m_cl_inc_ld_2_cout), .CLK(CLK), .Ii(I2_0_589fad62[2]),
    .LD(LD));  // open: Cout
  REG1m_CL_INC_LD reg1m_cl_inc_ld_2 (
    .Cout(reg1m_cl_inc_ld_2_cout), .Ai(A2_0_8a36edda[1]), .CL(CL), .INC(INC), .Ci(reg1m_cl_inc_ld_3_cout),
    .CLK(CLK), .Ii(I2_0_589fad62[1]), .LD(LD));
  REG1m_CL_INC_LD reg1m_cl_inc_ld_3 (
    .Cout(reg1m_cl_inc_ld_3_cout), .Ai(A2_0_8a36edda[0]), .CL(CL), .INC(INC), .Ci(INC), .CLK(CLK),
    .Ii(I2_0_589fad62[0]), .LD(LD));
endmodule

module REG4_CL_INC_LD (
  input  [3:0] I3_0_530b42ff,
  input  LD,
  input  CL,
  input  INC,
  input  CLK,
  output [3:0] A3_0_6aaf74d5
);

  wire reg2m_cl_inc_ld_2_cout;

  REG2m_CL_INC_LD reg2m_cl_inc_ld_1 (
    .A1_0_e4900909(A3_0_6aaf74d5[3:2]), .LD(LD), .CL(CL), .Cin(reg2m_cl_inc_ld_2_cout), .INC(INC), .CLK(CLK),
    .I1_0_431d2720(I3_0_530b42ff[3:2]));  // open: Cout
  REG2m_CL_INC_LD reg2m_cl_inc_ld_2 (
    .Cout(reg2m_cl_inc_ld_2_cout), .A1_0_e4900909(A3_0_6aaf74d5[1:0]), .LD(LD), .CL(CL), .Cin(INC),
    .INC(INC), .CLK(CLK), .I1_0_431d2720(I3_0_530b42ff[1:0]));
endmodule

module REG5_CL_INC_LD (
  input  [4:0] I4_0_01b0856d,
  input  LD,
  input  CL,
  input  INC,
  input  CLK,
  output [4:0] A4_0_c0bc1768
);

  wire reg4m_cl_inc_ld_1_cout;

  REG1m_CL_INC_LD reg1m_cl_inc_ld_1 (
    .Ai(A4_0_c0bc1768[4]), .CL(CL), .INC(INC), .Ci(reg4m_cl_inc_ld_1_cout), .CLK(CLK), .Ii(I4_0_01b0856d[4]),
    .LD(LD));  // open: Cout
  REG4m_CL_INC_LD reg4m_cl_inc_ld_1 (
    .Cout(reg4m_cl_inc_ld_1_cout), .A3_0_6aaf74d5(A4_0_c0bc1768[3:0]), .LD(LD), .CL(CL), .Cin(INC),
    .INC(INC), .CLK(CLK), .I3_0_530b42ff(I4_0_01b0856d[3:0]));
endmodule

module REG1_SR (
  input  IR,
  input  SR,
  input  CLK,
  output Ai
);

  wire and_1_out, and_2_out, or_1_out;

  and and_1 (and_1_out, IR, SR);
  and and_2 (and_2_out, ~SR, Ai);  // AND_Gate
  or or_1 (or_1_out, and_1_out, and_2_out);
  DFF dff_1 (.Q(Ai), .D(or_1_out), .CLK(CLK));  // open: notQ, Sd, Rd
endmodule

module REG2_SR (
  input  IR,
  input  SR,
  input  CLK,
  output [1:0] A1_0_e4900909
);

  REG1_SR reg1_sr_1 (.Ai(A1_0_e4900909[1]), .CLK(CLK), .IR(IR), .SR(SR));
  REG1_SR reg1_sr_2 (.Ai(A1_0_e4900909[0]), .CLK(CLK), .IR(A1_0_e4900909[1]), .SR(SR));
endmodule

module REG3_SR (
  input  IR,
  input  SR,
  input  CLK,
  output [2:0] A2_0_8a36edda
);

  REG1_SR reg1_sr_1 (.Ai(A2_0_8a36edda[2]), .CLK(CLK), .IR(IR), .SR(SR));
  REG2_SR reg2_sr_1 (.A1_0_e4900909(A2_0_8a36edda[1:0]), .SR(SR), .CLK(CLK), .IR(A2_0_8a36edda[2]));
endmodule

module REG4_SR (
  input  IR,
  input  SR,
  input  CLK,
  output [3:0] A3_0_6aaf74d5
);

  REG2_SR reg2_sr_1 (.A1_0_e4900909(A3_0_6aaf74d5[3:2]), .SR(SR), .CLK(CLK), .IR(IR));
  REG2_SR reg2_sr_2 (.A1_0_e4900909(A3_0_6aaf74d5[1:0]), .SR(SR), .CLK(CLK), .IR(A3_0_6aaf74d5[2]));
endmodule

module REG8_SR (
  input  IR,
  input  SR,
  input  CLK,
  output [7:0] A7_0_536de17e
);

  REG4_SR reg4_sr_1 (.A3_0_6aaf74d5(A7_0_536de17e[7:4]), .IR(IR), .SR(SR), .CLK(CLK));
  REG4_SR reg4_sr_2 (.A3_0_6aaf74d5(A7_0_536de17e[3:0]), .IR(A7_0_536de17e[4]), .SR(SR), .CLK(CLK));
endmodule

module REG1m_DEC_LD (
  input  Ii,
  input  LD,
  input  DEC,
  input  Ei,
  input  CLK,
  output Ai,
  output Eout
);

  wire and_1_out, and_2_out, and_3_out, or_1_out, xor_1_out;

  xor xor_1 (xor_1_out, Ei, Ai);
  and and_1 (and_1_out, DEC, xor_1_out);
  and and_2 (and_2_out, Ii, LD);
  and and_3 (and_3_out, ~LD, ~DEC, Ai);  // AND_Gate
  or or_1 (or_1_out, and_2_out, and_3_out, and_1_out);
  DFF dff_1 (.Q(Ai), .D(or_1_out), .CLK(CLK));  // open: notQ, Sd, Rd
  and and_4 (Eout, ~Ai, Ei);  // AND_Gate
endmodule

module REG2m_DEC_LD (
  input  [1:0] I1_0_431d2720,
  input  LD,
  input  Ein,
  input  DEC,
  input  CLK,
  output Eout,
  output [1:0] A1_0_e4900909
);

  wire reg1m_dec_ld_2_eout;

  REG1m_DEC_LD reg1m_dec_ld_1 (
    .Ai(A1_0_e4900909[1]), .Eout(Eout), .DEC(DEC), .Ei(reg1m_dec_ld_2_eout), .CLK(CLK),
    .Ii(I1_0_431d2720[1]), .LD(LD));
  REG1m_DEC_LD reg1m_dec_ld_2 (
    .Ai(A1_0_e4900909[0]), .Eout(reg1m_dec_ld_2_eout), .DEC(DEC), .Ei(Ein), .CLK(CLK), .Ii(I1_0_431d2720[0]),
    .LD(LD));
endmodule

module REG4m_DEC_LD (
  input  [3:0] I3_0_530b42ff,
  input  LD,
  input  Ein,
  input  DEC,
  input  CLK,
  output Eout,
  output [3:0] A3_0_6aaf74d5
);

  wire reg2m_dec_ld_2_eout;

  REG2m_DEC_LD reg2m_dec_ld_1 (
    .Eout(Eout), .A1_0_e4900909(A3_0_6aaf74d5[3:2]), .LD(LD), .Ein(reg2m_dec_ld_2_eout), .DEC(DEC),
    .CLK(CLK), .I1_0_431d2720(I3_0_530b42ff[3:2]));
  REG2m_DEC_LD reg2m_dec_ld_2 (
    .Eout(reg2m_dec_ld_2_eout), .A1_0_e4900909(A3_0_6aaf74d5[1:0]), .LD(LD), .Ein(Ein), .DEC(DEC), .CLK(CLK),
    .I1_0_431d2720(I3_0_530b42ff[1:0]));
endmodule

module REG1m_CL_INC (
  input  CL,
  input  INC,
  input  Ci,
  input  CLK,
  output Ai,
  output Cout
);

  wire and_1_out, and_2_out, or_1_out, xor_1_out;

  xor xor_1 (xor_1_out, Ci, Ai);
  and and_1 (and_1_out, INC, xor_1_out);
  and and_2 (and_2_out, ~CL, ~INC, Ai);  // AND_Gate
  or or_1 (or_1_out, and_2_out, and_1_out);
  DFF dff_1 (.Q(Ai), .D(or_1_out), .CLK(CLK));  // open: notQ, Sd, Rd
  and and_3 (Cout, Ai, Ci);
endmodule

module REG2m_CL_INC (
  input  CL,
  input  Cin,
  input  INC,
  input  CLK,
  output Cout,
  output [1:0] A1_0_e4900909
);

  wire reg1m_cl_inc_2_cout;

  REG1m_CL_INC reg1m_cl_inc_1 (
    .Cout(Cout), .Ai(A1_0_e4900909[1]), .Ci(reg1m_cl_inc_2_cout), .CLK(CLK), .CL(CL), .INC(INC));
  REG1m_CL_INC reg1m_cl_inc_2 (
    .Cout(reg1m_cl_inc_2_cout), .Ai(A1_0_e4900909[0]), .Ci(Cin), .CLK(CLK), .CL(CL), .INC(INC));
endmodule

module REG4m_CL_INC (
  input  CL,
  input  Cin,
  input  INC,
  input  CLK,
  output Cout,
  output [3:0] A3_0_6aaf74d5
);

  wire reg2m_cl_inc_2_cout;

  REG2m_CL_INC reg2m_cl_inc_1 (
    .Cout(Cout), .A1_0_e4900909(A3_0_6aaf74d5[3:2]), .CL(CL), .Cin(reg2m_cl_inc_2_cout), .INC(INC), .CLK(CLK));
  REG2m_CL_INC reg2m_cl_inc_2 (
    .Cout(reg2m_cl_inc_2_cout), .A1_0_e4900909(A3_0_6aaf74d5[1:0]), .CL(CL), .Cin(Cin), .INC(INC), .CLK(CLK));
endmodule

module REG1m_CL_INC_LD (
  input  Ii,
  input  LD,
  input  CL,
  input  INC,
  input  Ci,
  input  CLK,
  output Ai,
  output Cout
);

  wire and_1_out, and_2_out, and_3_out, or_1_out, xor_1_out;

  xor xor_1 (xor_1_out, Ci, Ai);
  and and_1 (and_1_out, INC, xor_1_out);
  and and_2 (and_2_out, Ii, LD);
  and and_3 (and_3_out, ~LD, ~CL, ~INC, Ai);  // AND_Gate
  or or_1 (or_1_out, and_2_out, and_3_out, and_1_out);
  DFF dff_1 (.Q(Ai), .D(or_1_out), .CLK(CLK));  // open: notQ, Sd, Rd
  and and_4 (Cout, Ai, Ci);
endmodule

module REG2m_CL_INC_LD (
  input  [1:0] I1_0_431d2720,
  input  LD,
  input  CL,
  input  Cin,
  input  INC,
  input  CLK,
  output Cout,
  output [1:0] A1_0_e4900909
);

  wire reg1m_cl_inc_ld_2_cout;

  REG1m_CL_INC_LD reg1m_cl_inc_ld_1 (
    .Cout(Cout), .Ai(A1_0_e4900909[1]), .CL(CL), .INC(INC), .Ci(reg1m_cl_inc_ld_2_cout), .CLK(CLK),
    .Ii(I1_0_431d2720[1]), .LD(LD));
  REG1m_CL_INC_LD reg1m_cl_inc_ld_2 (
    .Cout(reg1m_cl_inc_ld_2_cout), .Ai(A1_0_e4900909[0]), .CL(CL), .INC(INC), .Ci(Cin), .CLK(CLK),
    .Ii(I1_0_431d2720[0]), .LD(LD));
endmodule

module REG4m_CL_INC_LD (
  input  [3:0] I3_0_530b42ff,
  input  LD,
  input  CL,
  input  Cin,
  input  INC,
  input  CLK,
  output Cout,
  output [3:0] A3_0_6aaf74d5
);

  wire reg2m_cl_inc_ld_2_cout;

  REG2m_CL_INC_LD reg2m_cl_inc_ld_1 (
    .Cout(Cout), .A1_0_e4900909(A3_0_6aaf74d5[3:2]), .LD(LD), .CL(CL), .Cin(reg2m_cl_inc_ld_2_cout),
    .INC(INC), .CLK(CLK), .I1_0_431d2720(I3_0_530b42ff[3:2]));
  REG2m_CL_INC_LD reg2m_cl_inc_ld_2 (
    .Cout(reg2m_cl_inc_ld_2_cout), .A1_0_e4900909(A3_0_6aaf74d5[1:0]), .LD(LD), .CL(CL), .Cin(Cin),
    .INC(INC), .CLK(CLK), .I1_0_431d2720(I3_0_530b42ff[1:0]));
endmodule

module RisingEdge (
  input  INPUT,
  input  CLK,
  output OUTPUT
);

  wire dff_1_q, dff_2_q;

  DFF dff_1 (.Q(dff_1_q), .D(INPUT), .CLK(CLK));  // open: notQ, Sd, Rd
  DFF dff_2 (.Q(dff_2_q), .D(dff_1_q), .CLK(CLK));  // open: notQ, Sd, Rd
  and and_1 (OUTPUT, dff_1_q, ~dff_2_q);  // AND_Gate
endmodule

module FallingEdge (
  input  INPUT,
  input  CLK,
  output OUTPUT
);

  wire dff_1_q, dff_2_q;

  DFF dff_1 (.Q(dff_1_q), .D(INPUT), .CLK(CLK));  // open: notQ, Sd, Rd
  DFF dff_2 (.Q(dff_2_q), .D(dff_1_q), .CLK(CLK));  // open: notQ, Sd, Rd
  and and_1 (OUTPUT, ~dff_1_q, dff_2_q);  // AND_Gate
endmodule

module MP2_1b (
  input  En,
  input  I0,
  input  I1,
  input  S0,
  output Y
);

  wire and_1_out, and_2_out, not_1_out, or_1_out;

  Pull_Resistor #(.pull(1)) pull_resistor_1 (.node(En));
  not not_1 (not_1_out, S0);
  and and_1 (and_1_out, I0, not_1_out);
  and and_2 (and_2_out, I1, S0);
  or or_1 (or_1_out, and_1_out, and_2_out);
  and and_3 (Y, En, or_1_out);

  // Notes on the sheet:
  //   Ako En nije priključen (stanje visoke impednase - HiZ),
  //   uezti za podrazumevanu vrednost logičku jedinicu
endmodule

module MP2_8b (
  input  En,
  input  [7:0] in_2,
  input  [7:0] in_3,
  input  S0,
  output [7:0] out_5
);

  wire not_1_out;
  wire [7:0] and_1_out, and_2_out, bit_extender_1_out, bit_extender_2_out, bit_extender_3_out, or_1_out;

  Pull_Resistor #(.pull(1)) pull_resistor_1 (.node(En));
  assign bit_extender_1_out = {{7{S0}}, S0};  // Bit_Extender bit_extender_1
  assign bit_extender_2_out = {{7{not_1_out}}, not_1_out};  // Bit_Extender bit_extender_2
  not not_1 (not_1_out, S0);
  assign and_1_out = in_2 & bit_extender_2_out;  // AND_Gate and_1, 8 bits wide
  assign and_2_out = in_3 & bit_extender_1_out;  // AND_Gate and_2, 8 bits wide
  assign bit_extender_3_out = {{7{En}}, En};  // Bit_Extender bit_extender_3
  assign or_1_out = and_1_out | and_2_out;  // OR_Gate or_1, 8 bits wide
  assign out_5 = bit_extender_3_out & or_1_out;  // AND_Gate and_3, 8 bits wide

  // Notes on the sheet:
  //   I0
  //   7..0
  //   I1
  //   7..0
  //   Ako En nije priključen (stanje visoke impednase - HiZ),
  //   uezti za podrazumevanu vrednost logičku jedinicu
  //   Y
  //   7..0
endmodule

module MP2_16b (
  input  En,
  input  [15:0] in_2,
  input  [15:0] in_3,
  input  S0,
  output [15:0] out_5
);

  wire not_1_out;
  wire [15:0] and_1_out, and_2_out, bit_extender_1_out, bit_extender_2_out, bit_extender_3_out, or_1_out;

  Pull_Resistor #(.pull(1)) pull_resistor_1 (.node(En));
  assign bit_extender_1_out = {{15{S0}}, S0};  // Bit_Extender bit_extender_1
  assign bit_extender_2_out = {{15{not_1_out}}, not_1_out};  // Bit_Extender bit_extender_2
  not not_1 (not_1_out, S0);
  assign and_1_out = in_2 & bit_extender_2_out;  // AND_Gate and_1, 16 bits wide
  assign and_2_out = in_3 & bit_extender_1_out;  // AND_Gate and_2, 16 bits wide
  assign bit_extender_3_out = {{15{En}}, En};  // Bit_Extender bit_extender_3
  assign or_1_out = and_1_out | and_2_out;  // OR_Gate or_1, 16 bits wide
  assign out_5 = bit_extender_3_out & or_1_out;  // AND_Gate and_3, 16 bits wide

  // Notes on the sheet:
  //   I0
  //   15..0
  //   I1
  //   15..0
  //   Ako En nije priključen (stanje visoke impednase - HiZ),
  //   uezti za podrazumevanu vrednost logičku jedinicu
  //   Y
  //   15..0
endmodule

module MP4_1b (
  input  I0,
  input  I1,
  input  I2,
  input  I3,
  input  En,
  input  S0,
  input  S1,
  output Y
);

  wire mp2_1b_1_y, mp2_1b_3_y;

  MP2_1b mp2_1b_1 (.Y(mp2_1b_1_y), .I0(I0), .I1(I1), .S0(S0));  // open: En
  MP2_1b mp2_1b_2 (.Y(Y), .I0(mp2_1b_1_y), .I1(mp2_1b_3_y), .S0(S1), .En(En));
  MP2_1b mp2_1b_3 (.Y(mp2_1b_3_y), .I0(I2), .I1(I3), .S0(S0));  // open: En
endmodule

module MP4_8b (
  input  [7:0] I0,
  input  [7:0] I1,
  input  [7:0] I2,
  input  [7:0] I3,
  input  En,
  input  S0,
  input  S1,
  output [7:0] Y
);

  wire [7:0] mp2_8b_1_out_5, mp2_8b_3_out_5;

  Pull_Resistor #(.pull(1)) pull_resistor_1 (.node(En));
  MP2_8b mp2_8b_1 (.out_5(mp2_8b_1_out_5), .S0(S0), .in_2(I0), .in_3(I1));  // open: En
  MP2_8b mp2_8b_2 (.out_5(Y), .En(En), .S0(S1), .in_2(mp2_8b_1_out_5), .in_3(mp2_8b_3_out_5));
  MP2_8b mp2_8b_3 (.out_5(mp2_8b_3_out_5), .S0(S0), .in_2(I2), .in_3(I3));  // open: En

  // Notes on the sheet:
  //   Ako En nije priključen (stanje visoke impednase - HiZ),
  //   uezti za podrazumevanu vrednost logičku jedinicu
  //   7..0
  //   7..0
  //   7..0
  //   7..0
endmodule

module MP4_16b (
  input  [15:0] I0,
  input  [15:0] I1,
  input  [15:0] I2,
  input  [15:0] I3,
  input  En,
  input  S0,
  input  S1,
  output [15:0] Y
);

  wire [15:0] mp2_16b_1_out_5, mp2_16b_3_out_5;

  Pull_Resistor #(.pull(1)) pull_resistor_1 (.node(En));
  MP2_16b mp2_16b_1 (.out_5(mp2_16b_1_out_5), .S0(S0), .in_2(I0), .in_3(I1));  // open: En
  MP2_16b mp2_16b_2 (.out_5(Y), .En(En), .S0(S1), .in_2(mp2_16b_1_out_5), .in_3(mp2_16b_3_out_5));
  MP2_16b mp2_16b_3 (.out_5(mp2_16b_3_out_5), .S0(S0), .in_2(I2), .in_3(I3));  // open: En

  // Notes on the sheet:
  //   Ako En nije priključen (stanje visoke impednase - HiZ),
  //   uezti za podrazumevanu vrednost logičku jedinicu
  //   15..0
  //   15..0
  //   15..0
  //   15..0
endmodule

module DFF (
  input  D,
  input  CLK,
  input  Sd,
  input  Rd,
  output Q,
  output notQ
);

  wire not_1_out, not_2_out;

  not not_1 (not_1_out, Sd);
  not not_2 (not_2_out, Rd);
  D_Flip_Flop d_ff_1 (.D(D), .clk(CLK), .Q(Q), .Qn(notQ), .preset(not_1_out), .reset(not_2_out));
endmodule

module TFF (
  input  T,
  input  CLK,
  input  Sd,
  input  Rd,
  output Q,
  output notQ
);

  wire not_1_out, not_2_out;

  not not_1 (not_1_out, Sd);
  not not_2 (not_2_out, Rd);
  T_Flip_Flop t_ff_1 (.T(T), .clk(CLK), .Q(Q), .Qn(notQ), .reset(not_2_out), .preset(not_1_out));
endmodule

module RSFF (
  input  S,
  input  R,
  input  CLK,
  input  Sd,
  input  Rd,
  output Q,
  output notQ
);

  wire not_1_out, not_2_out;

  not not_1 (not_1_out, Sd);
  not not_2 (not_2_out, Rd);
  S_R_Flip_Flop s_r_ff_1 (.S(S), .R(R), .clk(CLK), .Q(Q), .reset(not_2_out), .Qn(notQ), .preset(not_1_out));
endmodule

module JKFF (
  input  J,
  input  K,
  input  CLK,
  input  Sd,
  input  Rd,
  output Q,
  output notQ
);

  wire not_1_out, not_2_out;

  not not_1 (not_1_out, Sd);
  not not_2 (not_2_out, Rd);
  J_K_Flip_Flop j_k_ff_1 (.J(J), .K(K), .clk(CLK), .Q(Q), .Qn(notQ), .preset(not_1_out), .reset(not_2_out));
endmodule

module SUB1 (
  input  Ein,
  input  A,
  input  B,
  output F,
  output Eout
);

  Subtractor #(.width(1)) subtractor_1 (.a(A), .b(B), .out(F), .bin(Ein), .bout(Eout));
endmodule

module SUB8 (
  input  E0,
  input  [7:0] A,
  input  [7:0] B,
  output [7:0] F,
  output E8
);

  Subtractor subtractor_1 (.a(A), .b(B), .out(F), .bin(E0), .bout(E8));
endmodule

module SUB16 (
  input  E0,
  input  [15:0] A,
  input  [15:0] B,
  output [15:0] F,
  output E16
);

  Subtractor #(.width(16)) subtractor_1 (.a(A), .b(B), .out(F), .bin(E0), .bout(E16));
endmodule

module INC1 (
  input  Cin,
  input  A,
  output F,
  output Cout
);

  xor xor_1 (F, Cin, A);
  and and_1 (Cout, Cin, A);
endmodule

module INC8 (
  input  [7:0] A,
  input  Cin,
  output Cout,
  output [7:0] F
);

  wire inc1_2_cout, inc1_3_cout, inc1_4_cout, inc1_5_cout, inc1_6_cout, inc1_7_cout, inc1_8_cout;

  INC1 inc1_1 (.Cout(Cout), .F(F[7]), .Cin(inc1_2_cout), .A(A[7]));
  INC1 inc1_2 (.Cout(inc1_2_cout), .F(F[6]), .Cin(inc1_3_cout), .A(A[6]));
  INC1 inc1_3 (.Cout(inc1_3_cout), .F(F[5]), .Cin(inc1_4_cout), .A(A[5]));
  INC1 inc1_4 (.Cout(inc1_4_cout), .F(F[4]), .Cin(inc1_5_cout), .A(A[4]));
  INC1 inc1_5 (.Cout(inc1_5_cout), .F(F[3]), .Cin(inc1_6_cout), .A(A[3]));
  INC1 inc1_6 (.Cout(inc1_6_cout), .F(F[2]), .Cin(inc1_7_cout), .A(A[2]));
  INC1 inc1_7 (.Cout(inc1_7_cout), .F(F[1]), .Cin(inc1_8_cout), .A(A[1]));
  INC1 inc1_8 (.Cout(inc1_8_cout), .F(F[0]), .Cin(Cin), .A(A[0]));

  // Notes on the sheet:
  //   7..0
  //   7..0
endmodule

module INC16 (
  input  [15:0] A,
  input  Cin,
  output Cout,
  output [15:0] F
);

  wire inc8_2_cout;

  INC8 inc8_1 (.Cout(Cout), .F(F[15:8]), .A(A[15:8]), .Cin(inc8_2_cout));
  INC8 inc8_2 (.Cout(inc8_2_cout), .F(F[7:0]), .A(A[7:0]), .Cin(Cin));

  // Notes on the sheet:
  //   15..0
  //   15..0
endmodule

module MEM2x8 (
  input  [7:0] DIN,
  input  CLK,
  input  WR_RD_9ce5c215,
  input  CS,
  input  A0,
  output [7:0] DOUT
);

  wire and_1_out, and_2_out, dc1_2_1_d0, dc1_2_1_d1, not_1_out;
  wire [7:0] controlled_buffer_1_out, reg8_ld_1_a7_0_536de17e, reg8_ld_2_a7_0_536de17e;

  not not_1 (not_1_out, WR_RD_9ce5c215);
  DC1_2 dc1_2_1 (.D0(dc1_2_1_d0), .D1(dc1_2_1_d1), .X0(A0), .En(CS));
  and and_1 (and_1_out, WR_RD_9ce5c215, dc1_2_1_d0);
  REG8_LD reg8_ld_1 (.A7_0_536de17e(reg8_ld_1_a7_0_536de17e), .LD(and_1_out), .CLK(CLK), .I7_0_76b06db5(DIN));
  assign controlled_buffer_1_out = dc1_2_1_d0 ? reg8_ld_1_a7_0_536de17e : 8'bz;  // Controlled_Buffer controlled_buffer_1
  assign DOUT = not_1_out ? controlled_buffer_1_out : 8'bz;  // Controlled_Buffer controlled_buffer_2
  REG8_LD reg8_ld_2 (.A7_0_536de17e(reg8_ld_2_a7_0_536de17e), .LD(and_2_out), .CLK(CLK), .I7_0_76b06db5(DIN));
  assign controlled_buffer_1_out = dc1_2_1_d1 ? reg8_ld_2_a7_0_536de17e : 8'bz;  // Controlled_Buffer controlled_buffer_3
  and and_2 (and_2_out, WR_RD_9ce5c215, dc1_2_1_d1);

  // Notes on the sheet:
  //   __
endmodule

module MEM4x8 (
  input  [7:0] DIN,
  input  WR_RD_9ce5c215,
  input  [1:0] A1_0_e4900909,
  input  CS,
  input  CLK,
  output [7:0] DOUT
);

  wire dc1_2_1_d0, dc1_2_1_d1;

  DC1_2 dc1_2_1 (.D0(dc1_2_1_d0), .D1(dc1_2_1_d1), .X0(A1_0_e4900909[1]), .En(CS));
  MEM2x8 mem2x8_1 (
    .DOUT(DOUT), .CLK(CLK), .WR_RD_9ce5c215(WR_RD_9ce5c215), .CS(dc1_2_1_d0), .A0(A1_0_e4900909[0]), .DIN(DIN));
  MEM2x8 mem2x8_2 (
    .DOUT(DOUT), .CLK(CLK), .WR_RD_9ce5c215(WR_RD_9ce5c215), .CS(dc1_2_1_d1), .A0(A1_0_e4900909[0]), .DIN(DIN));

  // Notes on the sheet:
  //   __
endmodule

module MEM8x8 (
  input  [7:0] DIN,
  input  WR_RD_9ce5c215,
  input  [2:0] A2_0_8a36edda,
  input  CS,
  input  CLK,
  output [7:0] DOUT
);

  wire dc1_2_1_d0, dc1_2_1_d1;

  DC1_2 dc1_2_1 (.D0(dc1_2_1_d0), .D1(dc1_2_1_d1), .X0(A2_0_8a36edda[2]), .En(CS));
  MEM4x8 mem4x8_1 (
    .DOUT(DOUT), .WR_RD_9ce5c215(WR_RD_9ce5c215), .A1_0_e4900909(A2_0_8a36edda[1:0]), .CS(dc1_2_1_d0),
    .CLK(CLK), .DIN(DIN));
  MEM4x8 mem4x8_2 (
    .DOUT(DOUT), .WR_RD_9ce5c215(WR_RD_9ce5c215), .A1_0_e4900909(A2_0_8a36edda[1:0]), .CS(dc1_2_1_d1),
    .CLK(CLK), .DIN(DIN));

  // Notes on the sheet:
  //   __
endmodule

module MEM16x8 (
  input  [7:0] DIN,
  input  WR_RD_9ce5c215,
  input  [3:0] A3_0_6aaf74d5,
  input  CS,
  input  CLK,
  output [7:0] DOUT
);

  wire dc1_2_1_d0, dc1_2_1_d1;

  DC1_2 dc1_2_1 (.D0(dc1_2_1_d0), .D1(dc1_2_1_d1), .X0(A3_0_6aaf74d5[3]), .En(CS));
  MEM8x8 mem8x8_1 (
    .DOUT(DOUT), .WR_RD_9ce5c215(WR_RD_9ce5c215), .A2_0_8a36edda(A3_0_6aaf74d5[2:0]), .CS(dc1_2_1_d0),
    .CLK(CLK), .DIN(DIN));
  MEM8x8 mem8x8_2 (
    .DOUT(DOUT), .WR_RD_9ce5c215(WR_RD_9ce5c215), .A2_0_8a36edda(A3_0_6aaf74d5[2:0]), .CS(dc1_2_1_d1),
    .CLK(CLK), .DIN(DIN));

  // Notes on the sheet:
  //   __
endmodule

module MEM32x8 (
  input  [4:0] A,
  input  WR_RD,
  input  [7:0] DIN,
  input  CS,
  input  CLK,
  output [7:0] out_6
);

  wire and_1_out;
  wire [7:0] ram_1_dout;

  RAM #(.addrWidth(5), .enables("line")) ram_1 (.addr(A), .we(and_1_out), .clk(CLK), .din(DIN), .dout(ram_1_dout));
  and and_1 (and_1_out, WR_RD, CS);
  Multiplexer #(.enable("false"), .width(8)) multiplexer_1 (.in1(ram_1_dout), .out(out_6), .sel(CS));  // open: in0
endmodule

module MEM64x8 (
  input  [5:0] A,
  input  WR_RD,
  input  [7:0] DIN,
  input  CS,
  input  CLK,
  output [7:0] out_6
);

  wire and_1_out;
  wire [7:0] ram_1_dout;

  RAM #(.addrWidth(6), .enables("line")) ram_1 (.addr(A), .we(and_1_out), .clk(CLK), .din(DIN), .dout(ram_1_dout));
  and and_1 (and_1_out, WR_RD, CS);
  Multiplexer #(.enable("false"), .width(8)) multiplexer_1 (.in1(ram_1_dout), .out(out_6), .sel(CS));  // open: in0
endmodule

module MEM128x8 (
  input  [6:0] A,
  input  WR_RD,
  input  [7:0] DIN,
  input  CS,
  input  CLK,
  output [7:0] out_6
);

  wire and_1_out;
  wire [7:0] ram_1_dout;

  RAM #(.addrWidth(7), .enables("line")) ram_1 (.addr(A), .we(and_1_out), .clk(CLK), .din(DIN), .dout(ram_1_dout));
  and and_1 (and_1_out, WR_RD, CS);
  Multiplexer #(.enable("false"), .width(8)) multiplexer_1 (.in1(ram_1_dout), .out(out_6), .sel(CS));  // open: in0
endmodule

module MEM256x8 (
  input  [7:0] A,
  input  WR_RD,
  input  [7:0] DIN,
  input  CS,
  input  CLK,
  output [7:0] out_6
);

  wire and_1_out;
  wire [7:0] ram_1_dout;

  RAM #(.enables("line")) ram_1 (.addr(A), .we(and_1_out), .clk(CLK), .din(DIN), .dout(ram_1_dout));
  and and_1 (and_1_out, WR_RD, CS);
  Multiplexer #(.enable("false"), .width(8)) multiplexer_1 (.in1(ram_1_dout), .out(out_6), .sel(CS));  // open: in0
endmodule

module MEM512x8 (
  input  [8:0] A,
  input  WR_RD,
  input  [7:0] DIN,
  input  CS,
  input  CLK,
  output [7:0] out_6
);

  wire and_1_out;
  wire [7:0] ram_1_dout;

  RAM #(.addrWidth(9), .enables("line")) ram_1 (.addr(A), .we(and_1_out), .clk(CLK), .din(DIN), .dout(ram_1_dout));
  and and_1 (and_1_out, WR_RD, CS);
  Multiplexer #(.enable("false"), .width(8)) multiplexer_1 (.in1(ram_1_dout), .out(out_6), .sel(CS));  // open: in0
endmodule

module MEM1Kx8 (
  input  [9:0] A,
  input  WR_RD,
  input  [7:0] DIN,
  input  CS,
  input  CLK,
  output [7:0] DOUT
);

  wire and_1_out;
  wire [7:0] ram_1_dout;

  RAM #(.addrWidth(10), .enables("line")) ram_1 (.addr(A), .we(and_1_out), .clk(CLK), .din(DIN), .dout(ram_1_dout));
  and and_1 (and_1_out, WR_RD, CS);
  Multiplexer #(.enable("false"), .width(8)) multiplexer_1 (.in1(ram_1_dout), .out(DOUT), .sel(CS));  // open: in0
endmodule
