// Logisim project GPR8x16.circ as structural Verilog: 2 circuits, main circuit GPR8x16
module GPR8x16 (
  input  [2:0] ADR,
  input  WR,
  input  [15:0] DIN,
  input  CLK,
  output [15:0] out_5
);

  wire and_1_out, and_2_out, and_3_out, and_4_out, and_5_out, and_6_out, and_7_out, and_8_out, CS0, CS1, CS2,
       CS3, CS4, CS5, CS6, CS7;
  wire [15:0] reg16_inc_ld_dec_n_1_a, reg16_inc_ld_dec_n_2_a, reg16_inc_ld_dec_n_3_a, reg16_inc_ld_dec_n_4_a,
       reg16_inc_ld_dec_n_5_a, reg16_inc_ld_dec_n_6_a, reg16_inc_ld_dec_n_7_a, reg16_inc_ld_dec_n_8_a;

  Decoder #(.select(3), .enable("false")) decoder_1 (
    .out0(CS0), .out1(CS1), .out2(CS2), .out3(CS3), .out4(CS4), .out5(CS5), .out6(CS6), .out7(CS7), .sel(ADR));
  and and_1 (and_1_out, WR, CS0);
  and and_2 (and_2_out, WR, CS1);
  and and_3 (and_3_out, WR, CS2);
  and and_4 (and_4_out, WR, CS3);
  REG16_INC_LD_DEC_N reg16_inc_ld_dec_n_1 (
    .LD(and_1_out), .CLK(CLK), .I(DIN), .A(reg16_inc_ld_dec_n_1_a));  // open: INC, DEC, mr
  assign out_5 = CS0 ? reg16_inc_ld_dec_n_1_a : 16'bz;  // Controlled_Buffer controlled_buffer_1
  REG16_INC_LD_DEC_N reg16_inc_ld_dec_n_2 (
    .LD(and_2_out), .CLK(CLK), .I(DIN), .A(reg16_inc_ld_dec_n_2_a));  // open: INC, DEC, mr
  assign out_5 = CS1 ? reg16_inc_ld_dec_n_2_a : 16'bz;  // Controlled_Buffer controlled_buffer_2
  REG16_INC_LD_DEC_N reg16_inc_ld_dec_n_3 (
    .LD(and_3_out), .CLK(CLK), .I(DIN), .A(reg16_inc_ld_dec_n_3_a));  // open: INC, DEC, mr
  assign out_5 = CS2 ? reg16_inc_ld_dec_n_3_a : 16'bz;  // Controlled_Buffer controlled_buffer_3
  REG16_INC_LD_DEC_N reg16_inc_ld_dec_n_4 (
    .LD(and_4_out), .CLK(CLK), .I(DIN), .A(reg16_inc_ld_dec_n_4_a));  // open: INC, DEC, mr
  assign out_5 = CS3 ? reg16_inc_ld_dec_n_4_a : 16'bz;  // Controlled_Buffer controlled_buffer_4
  and and_5 (and_5_out, WR, CS4);
  REG16_INC_LD_DEC_N reg16_inc_ld_dec_n_5 (
    .LD(and_5_out), .CLK(CLK), .I(DIN), .A(reg16_inc_ld_dec_n_5_a));  // open: INC, DEC, mr
  assign out_5 = CS4 ? reg16_inc_ld_dec_n_5_a : 16'bz;  // Controlled_Buffer controlled_buffer_5
  and and_6 (and_6_out, WR, CS5);
  REG16_INC_LD_DEC_N reg16_inc_ld_dec_n_6 (
    .LD(and_6_out), .CLK(CLK), .I(DIN), .A(reg16_inc_ld_dec_n_6_a));  // open: INC, DEC, mr
  assign out_5 = CS5 ? reg16_inc_ld_dec_n_6_a : 16'bz;  // Controlled_Buffer controlled_buffer_6
  and and_7 (and_7_out, WR, CS6);
  REG16_INC_LD_DEC_N reg16_inc_ld_dec_n_7 (
    .LD(and_7_out), .CLK(CLK), .I(DIN), .A(reg16_inc_ld_dec_n_7_a));  // open: INC, DEC, mr
  assign out_5 = CS6 ? reg16_inc_ld_dec_n_7_a : 16'bz;  // Controlled_Buffer controlled_buffer_7
  and and_8 (and_8_out, WR, CS7);
  REG16_INC_LD_DEC_N reg16_inc_ld_dec_n_8 (
    .LD(and_8_out), .CLK(CLK), .I(DIN), .A(reg16_inc_ld_dec_n_8_a));  // open: INC, DEC, mr
  assign out_5 = CS7 ? reg16_inc_ld_dec_n_8_a : 16'bz;  // Controlled_Buffer controlled_buffer_8

  // Other names for the same wires on the sheet: DOUT[15:0] = out_5; ld = WR
endmodule

module REG16_INC_LD_DEC_N (
  input  LD,
  input  INC,
  input  DEC,
  input  mr,
  input  CLK,
  input  [15:0] I,
  output [15:0] A
);

  wire not_1_out, or_1_out, or_2_out;

  Pull_Resistor pull_resistor_1 (.node(LD));
  Pull_Resistor pull_resistor_2 (.node(INC));
  Pull_Resistor pull_resistor_3 (.node(DEC));
  Pull_Resistor #(.pull(1)) pull_resistor_4 (.node(mr));
  or or_1 (or_1_out, DEC, LD);
  or or_2 (or_2_out, DEC, INC);
  Counter #(.width(16), .max('hffff)) counter_1 (
    .load(or_1_out), .D(I), .count(or_2_out), .Q(A), .clk(CLK), .clr(not_1_out));  // open: carry
  not not_1 (not_1_out, mr);
endmodule
