// Logisim project ORT2 K1 2013 Logisim-evolution.circ as structural Verilog: 4 circuits, main circuit main
module main (
  input  in_1,
  input  in_2,
  input  [15:0] in_3,
  output out_4,
  output out_5,
  output out_6
);

  wire clock_1_out;

  Clock clock_1 (.out(clock_1_out));
  P p_1 (.SPB(in_1), .CAP(in_2), .DAP(in_3), .CLK(clock_1_out), .CPB(out_4), .DPB(out_5), .SPA(out_6));
endmodule

module P (
  input  SPB,
  input  CAP,
  input  [15:0] DAP,
  input  CLK,
  output CPB,
  output DPB,
  output SPA
);

  wire clA, clCOUNT, clMAX, clREZ, control, decSC, ldA, ldCNT, ldSC, not_1_out, S0, SC0, slREZ;
  wire [1:0] Iin, Iout;

  P_upravljacka p_upravljacka_1 (
    .Iin(Iout), .SPB(SPB), .SC0(SC0), .CAP(CAP), .clA(clA), .control(control), .clCOUNT(clCOUNT),
    .clREZ(clREZ), .clMAX(clMAX), .SPA(SPA), .ldA(ldA), .ldSC(ldSC), .ldCNT(ldCNT), .decSC(decSC),
    .Iout(Iin), .S0(S0), .CPB(CPB), .slREZ(clREZ));
  REG2_CL_INC_LD reg2_cl_inc_ld_1 (
    .A1_0_e4900909(Iout), .INC(not_1_out), .CLK(CLK), .I1_0_431d2720(Iin), .LD(ldCNT));  // open: CL
  not not_1 (not_1_out, ldCNT);
  P_operaciona p_operaciona_1 (
    .S0(S0), .clA(clA), .ldA(ldA), .ldSC(ldSC), .SPB(SPB), .DAP(DAP), .decSC(decSC), .CLK(CLK),
    .control(control), .clREZ(clREZ), .clMAX(clMAX), .slREZ(slREZ), .clCOUNT(clCOUNT), .DPB(DPB));

  // Notes on the sheet:
  //   Uređaj A
  //   Uređaj B
endmodule

module P_operaciona (
  input  S0,
  input  clA,
  input  ldA,
  input  ldSC,
  input  SPB,
  input  [15:0] DAP,
  input  decSC,
  input  CLK,
  input  control,
  input  clREZ,
  input  clMAX,
  input  slREZ,
  input  clCOUNT,
  output DPB
);

  wire and_1_out, and_2_out, and_3_out, and_4_out, comparator_2_gt, Less, or_1_out, Same, SC0;
  wire [7:0] COUNT, multiplexer_1_out, reg8_1_i, reg8_2_i;
  wire [14:0] reg16_2_i;
  wire [15:0] A;

  REG16 reg16_1 (.I(A), .A(DAP), .CL(clA), .CLK(CLK), .LD(ldA));  // open: Cout, Eout, SL, IL, SR, IR, DEC, INC
  Comparator #(.width(16)) comparator_1 (.a(A), .b(DAP), .eq(Same));  // open: gt, lt
  REG16 reg16_2 (
    .I({DPB, reg16_2_i}), .A(A), .SL(slREZ), .CL(clREZ), .CLK(CLK), .LD(and_1_out));  // open: Cout, Eout, IL, SR, IR, DEC, INC
  and and_1 (and_1_out, ~Same, Less, control);  // AND_Gate
  and and_2 (and_2_out, control, ~Same);  // AND_Gate
  Multiplexer #(.width(8), .enable("false")) multiplexer_1 (
    .in0({8{1'b1}}), .in1(8'hf), .out(multiplexer_1_out), .sel(S0));
  REG8 reg8_1 (
    .I(reg8_1_i), .LD(ldSC), .DEC(decSC), .CLK(CLK), .A(multiplexer_1_out));  // open: Cout, Eout, CL, SL, IL, SR, IR, INC
  REG8 reg8_2 (
    .I(reg8_2_i), .CL(clMAX), .LD(and_3_out), .CLK(CLK), .A(COUNT));  // open: Cout, Eout, SL, IL, SR, IR, DEC, INC
  or or_1 (or_1_out, clCOUNT, and_2_out);
  REG8 reg8_3 (.I(COUNT), .CL(or_1_out), .INC(and_4_out), .CLK(CLK));  // open: Cout, Eout, LD, SL, IL, SR, IR, DEC, A
  and and_3 (and_3_out, ~Same, Less, control);  // AND_Gate
  not not_1 (Less, comparator_2_gt);
  Comparator comparator_2 (.a(reg8_2_i), .b(COUNT), .gt(comparator_2_gt));  // open: eq, lt
  and and_4 (and_4_out, Same, control);
  and and_5 (SC0, ~reg8_1_i[0], ~reg8_1_i[1], ~reg8_1_i[2], ~reg8_1_i[3], ~reg8_1_i[4], ~reg8_1_i[5], ~reg8_1_i[6], ~reg8_1_i[7]);  // AND_Gate

  // Other names for the same wires on the sheet: A15 = DPB
endmodule

module P_upravljacka (
  input  [1:0] Iin,
  input  SPB,
  input  SC0,
  input  CAP,
  output clA,
  output control,
  output clCOUNT,
  output clREZ,
  output clMAX,
  output SPA,
  output ldA,
  output ldSC,
  output ldCNT,
  output decSC,
  output [1:0] Iout,
  output S0,
  output CPB,
  output slREZ
);

  wire and_1_out, and_2_out, and_7_out, or_1_out, or_3_out, T2;

  Decoder #(.select(2), .enable("false")) decoder_1 (.out0(clA), .out1(SPA), .out2(T2), .sel(Iin));  // open: out3
  and and_1 (and_1_out, CAP, ~SC0);  // AND_Gate
  and and_2 (and_2_out, SPB, ~SC0);  // AND_Gate
  and and_3 (Iout[0], SPA, or_1_out);
  or or_1 (or_1_out, ~CAP, and_1_out);  // OR_Gate
  or or_2 (ldCNT, Iout[0], T2);
  and and_4 (Iout[1], T2, or_3_out);
  or or_3 (or_3_out, ~SPB, and_2_out);  // OR_Gate
  and and_5 (control, SPA, CAP);
  and and_6 (S0, control, SC0);
  and and_7 (and_7_out, control, ~SC0);  // AND_Gate
  and and_8 (CPB, T2, SPB);
  or or_4 (ldSC, clA, S0);
  or or_5 (decSC, and_7_out, CPB);

  assign clCOUNT = clA;
  assign clMAX = clA;
  assign clREZ = clA;
  assign ldA = control;
  assign slREZ = CPB;

  // Other names for the same wires on the sheet: T0 = clA; T1 = SPA
endmodule
