// Logisim project ORT2 K1 2013 Logisim.circ as structural Verilog: 1 circuit, main circuit main
module main (
  input  CAP,
  input  SPB,
  input  [15:0] in_3
);

  wire A15, and_1_out, and_2_out, and_3_out, and_4_out, and_7_out, and_9_out, and_11_out, clA, CLK,
       comparator_2_eq, comparator_2_lt, control, CPB, decSC, I0, I1, ldCNT, ldSC, Less, not_1_out, or_1_out,
       or_2_out, or_3_out, S0, Same, SC0, SPA, T2;
  wire [1:0] reg2_cl_inc_ld_1_a1_0_e4900909;
  wire [7:0] mp2_8b_1_y, reg8_1_i, reg8_2_i, reg8_3_i;
  wire [14:0] reg16_1_i;
  wire [15:0] reg16_2_i;

  Clock clock_1 (.out(CLK));
  REG2_CL_INC_LD reg2_cl_inc_ld_1 (
    .A1_0_e4900909(reg2_cl_inc_ld_1_a1_0_e4900909), .CL(1'b0), .INC(not_1_out), .CLK(CLK),
    .I1_0_431d2720({I1, I0}), .LD(ldCNT));
  REG16 reg16_1 (
    .I({A15, reg16_1_i}), .A(reg16_2_i), .SL(CPB), .IL(1'b0), .SR(1'b0), .IR(1'b0), .DEC(1'b0), .INC(1'b0),
    .CL(clA), .CLK(CLK), .LD(and_1_out));  // open: Cout, Eout
  not not_1 (not_1_out, ldCNT);
  DC2_4 dc2_4_1 (.D0(clA), .D1(SPA), .D2(T2), .X1_0_c7335de0(reg2_cl_inc_ld_1_a1_0_e4900909), .En(1'b1));  // open: D3
  and and_1 (and_1_out, ~Same, Less, control);  // AND_Gate
  Comparator #(.width(16)) comparator_1 (.a(reg16_2_i), .b(in_3), .eq(Same));  // open: gt, lt
  and and_2 (and_2_out, control, ~Same);  // AND_Gate
  or or_1 (or_1_out, ~CAP, and_3_out);  // OR_Gate
  and and_3 (and_3_out, CAP, ~SC0);  // AND_Gate
  or or_2 (or_2_out, ~SPB, and_4_out);  // OR_Gate
  and and_4 (and_4_out, SPB, ~SC0);  // AND_Gate
  REG16 reg16_2 (
    .I(reg16_2_i), .A(in_3), .SL(1'b0), .IL(1'b0), .SR(1'b0), .IR(1'b0), .DEC(1'b0), .INC(1'b0), .CL(clA),
    .CLK(CLK), .LD(control));  // open: Cout, Eout
  or or_3 (or_3_out, clA, and_2_out);
  and and_5 (I0, SPA, or_1_out);
  or or_4 (ldCNT, I0, T2);
  and and_6 (I1, T2, or_2_out);
  REG8 reg8_1 (
    .I(reg8_1_i), .CL(or_3_out), .LD(1'b0), .SL(1'b0), .IL(1'b0), .SR(1'b0), .IR(1'b0), .DEC(1'b0),
    .INC(and_7_out), .CLK(CLK));  // open: Cout, Eout, A
  REG8 reg8_2 (
    .I(reg8_2_i), .CL(1'b0), .LD(ldSC), .SL(1'b0), .IL(1'b0), .SR(1'b0), .IR(1'b0), .DEC(decSC), .INC(1'b0),
    .CLK(CLK), .A(mp2_8b_1_y));  // open: Cout, Eout
  and and_7 (and_7_out, Same, control);
  MP2_8b mp2_8b_1 (.Y(mp2_8b_1_y), .En(1'b1), .S1(S0), .I0({8{1'b1}}), .I1(8'hf));
  and and_8 (SC0, ~reg8_2_i[0], ~reg8_2_i[1], ~reg8_2_i[2], ~reg8_2_i[3], ~reg8_2_i[4], ~reg8_2_i[5], ~reg8_2_i[6], ~reg8_2_i[7]);  // AND_Gate
  REG8 reg8_3 (
    .I(reg8_3_i), .CL(clA), .LD(and_11_out), .SL(1'b0), .IL(1'b0), .SR(1'b0), .IR(1'b0), .DEC(1'b0),
    .INC(1'b0), .CLK(CLK), .A(reg8_1_i));  // open: Cout, Eout
  Comparator comparator_2 (.a(reg8_3_i), .b(reg8_1_i), .eq(comparator_2_eq), .lt(comparator_2_lt));  // open: gt
  and and_9 (and_9_out, control, ~SC0);  // AND_Gate
  and and_10 (CPB, T2, SPB);
  and and_11 (and_11_out, ~Same, Less, control);  // AND_Gate
  or or_5 (Less, comparator_2_eq, comparator_2_lt);
  and and_12 (control, SPA, CAP);
  and and_13 (S0, control, SC0);
  or or_6 (decSC, and_9_out, CPB);
  or or_7 (ldSC, clA, S0);

  // Other names for the same wires on the sheet: clCOUNT = clA; clMAX = clA; clREZ = clA; T0 = clA; ldA = control;
  //   slREZ = CPB; T1 = SPA

  // Notes on the sheet:
  //   DAP15..0
  //   UA
  //   P
  //   SPA
  //   UPRAVLJACKA JEDINICA
  //   K1 14/15
  //   UB
  //   CPB
  //   DPB0
endmodule
