// Logisim project ORT2 K1 2016 Logisim-evolution.circ as structural Verilog: 1 circuit, main circuit main
module main (
  input  CAP,
  input  SPB,
  input  [7:0] in_3,
  input  [2:0] DAP10__8,
  output CPB,
  output DPB
);

  wire A7, and_4_out, and_5_out, and_6_out, and_7_out, and_8_out, and_9_out, and_11_out, BR0, BR1, BROJAC0,
       CLK, decBR, decBROJAC, I0, I1, izlS0, ldA, ldBR, ldCNT, ldZNAK, not_1_out, or_1_out, or_2_out, slA,
       SPA, T3, ulS0, ZNAK;
  wire [1:0] reg2_cl_inc_ld_1_a1_0_e4900909;
  wire [2:0] reg3_dec_ld_1_a2_0_8a36edda;
  wire [3:0] reg4m_dec_ld_1_a3_0_6aaf74d5;
  wire [6:0] reg8_ld_sl_sr_1_a7_0_536de17e;
  wire [7:0] add8_1_f, mp2_8b_1_out_5, not_2_out;

  Clock clock_1 (.out(CLK));
  and and_1 (BR0, ~DAP10__8[0], ~DAP10__8[1], ~DAP10__8[2]);  // AND_Gate
  REG2_CL_INC_LD reg2_cl_inc_ld_1 (
    .A1_0_e4900909(reg2_cl_inc_ld_1_a1_0_e4900909), .CL(1'b0), .INC(not_1_out), .CLK(CLK),
    .I1_0_431d2720({I1, I0}), .LD(ldCNT));
  not not_1 (not_1_out, ldCNT);
  DC2_4 dc2_4_1 (.D0(SPA), .D1(decBR), .D2(ldZNAK), .D3(T3), .X1_0_c7335de0(reg2_cl_inc_ld_1_a1_0_e4900909), .En(1'b1));
  REG3_DEC_LD reg3_dec_ld_1 (
    .A2_0_8a36edda(reg3_dec_ld_1_a2_0_8a36edda), .DEC(decBR), .CLK(CLK), .I2_0_589fad62(DAP10__8), .LD(ldBR));
  REG4m_DEC_LD reg4m_dec_ld_1 (
    .A3_0_6aaf74d5(reg4m_dec_ld_1_a3_0_6aaf74d5), .LD(ldBR), .Ein(decBROJAC), .DEC(decBROJAC), .CLK(CLK),
    .I3_0_530b42ff(4'b1000));  // open: Eout
  and and_2 (BR1, reg3_dec_ld_1_a2_0_8a36edda[0], ~reg3_dec_ld_1_a2_0_8a36edda[1], ~reg3_dec_ld_1_a2_0_8a36edda[2]);  // AND_Gate
  and and_3 (BROJAC0, ~reg4m_dec_ld_1_a3_0_6aaf74d5[0], ~reg4m_dec_ld_1_a3_0_6aaf74d5[1], ~reg4m_dec_ld_1_a3_0_6aaf74d5[2], ~reg4m_dec_ld_1_a3_0_6aaf74d5[3]);  // AND_Gate
  MP2_8b mp2_8b_1 (.out_5(mp2_8b_1_out_5), .En(1'b1), .S0(ulS0), .in_2(in_3), .in_3(add8_1_f));
  REG8_LD_SL_SR reg8_ld_sl_sr_1 (
    .A7_0_536de17e({A7, reg8_ld_sl_sr_1_a7_0_536de17e}), .IR(1'b0), .SR(1'b0), .IL(1'b0), .SL(slA),
    .CLK(CLK), .I7_0_76b06db5(mp2_8b_1_out_5), .LD(ldA));
  assign not_2_out = ~{A7, reg8_ld_sl_sr_1_a7_0_536de17e};  // NOT_Gate not_2, 8 bits wide
  ADD8 add8_1 (.F(add8_1_f), .A(not_2_out), .B(8'h1), .C0(1'b0));  // open: C8
  REG1_LD reg1_ld_1 (.Ai(ZNAK), .CLK(CLK), .Ii(A7), .LD(ldZNAK));
  or or_1 (or_1_out, ~CAP, and_4_out);  // OR_Gate
  and and_4 (and_4_out, BR0, CAP);
  and and_5 (and_5_out, SPA, or_1_out);
  and and_6 (and_6_out, decBR, ~BR1);  // AND_Gate
  and and_7 (and_7_out, T3, or_2_out);
  or or_2 (or_2_out, ~SPB, ~BROJAC0);  // OR_Gate
  and and_8 (and_8_out, BR0, CAP);
  and and_9 (and_9_out, SPA, and_8_out);
  MP2_1b mp2_1b_1 (.Y(DPB), .I0(A7), .I1(ZNAK), .S0(izlS0), .En(1'b1));
  or or_3 (ldCNT, and_5_out, and_6_out, and_7_out);
  or or_4 (I0, and_6_out, and_7_out);
  or or_5 (I1, and_9_out, and_7_out);
  and and_10 (ldBR, SPA, CAP);
  and and_11 (and_11_out, ldZNAK, A7);
  and and_12 (ulS0, ldZNAK, A7);
  and and_13 (decBROJAC, T3, SPB);
  and and_14 (izlS0, BROJAC0, CPB);
  or or_6 (ldA, ldBR, and_11_out);
  and and_15 (CPB, T3, SPB);
  or or_7 (slA, decBR, decBROJAC);

  // Other names for the same wires on the sheet: T1 = decBR; ldBROJAC = ldBR; T2 = ldZNAK; T0 = SPA

  // Notes on the sheet:
  //   DAP7..0
  //   UA
  //   P
  //   SPA
  //   UPRAVLJACKA JEDINICA
  //   UB
endmodule
