// Logisim project ORT2 K1 2016 Logisim.circ as structural Verilog: 1 circuit, main circuit main
module main (
  input  CAP,
  input  SPB,
  input  [7:0] in_3,
  input  [2:0] DAP10__8,
  output DPB
);

  wire A7, and_4_out, and_5_out, and_6_out, and_7_out, and_8_out, and_9_out, and_11_out, BR0, BR1, BROJAC0,
       CLK, CPB, decBR, decBROJAC, I0, I1, izlS0, ldA, ldBR, ldCNT, ldZNAK, not_1_out, or_1_out, or_2_out,
       slA, SPA, T3, ulS0, ZNAK;
  wire [1:0] reg2_cl_inc_ld_1_a1__0;
  wire [2:0] reg3_dec_ld_1_a2__0;
  wire [3:0] reg4m_dec_ld_1_a3__0;
  wire [6:0] reg8_ld_sl_sr_1_a7__0;
  wire [7:0] add8_1_f, mp2_8b_1_out_5, not_2_out;

  Clock clock_1 (.out(CLK));
  and and_1 (BR0, ~DAP10__8[0], ~DAP10__8[1], ~DAP10__8[2]);  // AND_Gate
  REG2_CL_INC_LD reg2_cl_inc_ld_1 (
    .I1__0({I1, I0}), .LD(ldCNT), .CL(1'b0), .INC(not_1_out), .CLK(CLK), .A1__0(reg2_cl_inc_ld_1_a1__0));
  not not_1 (not_1_out, ldCNT);
  DC2_4 dc2_4_1 (.En(1'b1), .X1__0(reg2_cl_inc_ld_1_a1__0), .D0(SPA), .D1(decBR), .D2(ldZNAK), .D3(T3));
  REG3_DEC_LD reg3_dec_ld_1 (.I2__0(DAP10__8), .LD(ldBR), .DEC(decBR), .CLK(CLK), .A2__0(reg3_dec_ld_1_a2__0));
  REG4m_DEC_LD reg4m_dec_ld_1 (
    .I3__0(4'b1000), .LD(ldBR), .Ein(decBROJAC), .DEC(decBROJAC), .CLK(CLK), .A3__0(reg4m_dec_ld_1_a3__0));  // open: Eout
  and and_2 (BR1, reg3_dec_ld_1_a2__0[0], ~reg3_dec_ld_1_a2__0[1], ~reg3_dec_ld_1_a2__0[2]);  // AND_Gate
  and and_3 (BROJAC0, ~reg4m_dec_ld_1_a3__0[0], ~reg4m_dec_ld_1_a3__0[1], ~reg4m_dec_ld_1_a3__0[2], ~reg4m_dec_ld_1_a3__0[3]);  // AND_Gate
  MP2_8b mp2_8b_1 (.in_2(in_3), .in_3(add8_1_f), .S0(ulS0), .out_5(mp2_8b_1_out_5), .En(1'b1));
  REG8_LD_SL_SR reg8_ld_sl_sr_1 (
    .I7__0(mp2_8b_1_out_5), .LD(ldA), .IR(1'b0), .SR(1'b0), .IL(1'b0), .SL(slA), .CLK(CLK),
    .A7__0({A7, reg8_ld_sl_sr_1_a7__0}));
  assign not_2_out = ~{A7, reg8_ld_sl_sr_1_a7__0};  // NOT_Gate not_2, 8 bits wide
  ADD8 add8_1 (.C0(1'b0), .A(not_2_out), .B(8'h1), .F(add8_1_f));  // open: C8
  REG1_LD reg1_ld_1 (.Ii(A7), .LD(ldZNAK), .CLK(CLK), .Ai(ZNAK));
  or or_1 (or_1_out, ~CAP, and_4_out);  // OR_Gate
  and and_4 (and_4_out, BR0, CAP);
  and and_5 (and_5_out, SPA, or_1_out);
  and and_6 (and_6_out, decBR, ~BR1);  // AND_Gate
  and and_7 (and_7_out, T3, or_2_out);
  or or_2 (or_2_out, ~SPB, ~BROJAC0);  // OR_Gate
  and and_8 (and_8_out, BR0, CAP);
  and and_9 (and_9_out, SPA, and_8_out);
  MP2_1b mp2_1b_1 (.I0(A7), .I1(ZNAK), .S0(izlS0), .Y(DPB), .En(1'b1));
  or or_3 (ldCNT, and_5_out, and_6_out, and_7_out);
  or or_4 (I0, and_6_out, and_7_out);
  or or_5 (I1, and_9_out, and_7_out);
  and and_10 (ldBR, SPA, CAP);
  and and_11 (and_11_out, ldZNAK, A7);
  and and_12 (ulS0, ldZNAK, A7);
  and and_13 (decBROJAC, T3, SPB);
  and and_14 (izlS0, BROJAC0, CPB);
  or or_6 (ldA, ldBR, and_11_out);
  and and_15 (CPB, T3, SPB);
  or or_7 (slA, decBR, decBROJAC);

  // Other names for the same wires on the sheet: T1 = decBR; ldBROJAC = ldBR; T2 = ldZNAK; T0 = SPA

  // Notes on the sheet:
  //   DAP7..0
  //   UA
  //   P
  //   SPA
  //   UPRAVLJACKA JEDINICA
  //   UB
  //   CPB
endmodule
