// Logisim project ORT2 K1 2018 Logisim-evolution.circ as structural Verilog
module P_operaciona (
  input  [15:0] DAP,
  input  CLK,
  input  clADR,
  input  incADR,
  input  decADR,
  input  wrMEM,
  input  ldN,
  input  S0,
  input  S1,
  input  ldSC,
  input  decSC,
  output [13:0] DPB,
  output N0,
  output SC0
);

  wire or_1_out;
  wire [13:0] adder_1_out, adder_2_out, and_1_out, multiplexer_2_out;
  wire [15:0] multiplexer_1_out, reg16_1_i, reg16_2_i, subtractor_1_out;
  wire [15:1] N;

  REG16_LD reg16_ld_1 (.A15_0_fec680c4({N, N0}), .LD(ldN), .CLK(CLK), .I15_0_dbedc2e3(DAP));
  Multiplexer #(.enable("false"), .width(16)) multiplexer_1 (
    .in0({N, N0}), .in1(DAP), .out(multiplexer_1_out), .sel(S1));
  Subtractor #(.width(16)) subtractor_1 (
    .a({multiplexer_1_out[15:1], 1'b0}), .b(16'h1), .out(subtractor_1_out));  // open: bin, bout
  REG16 reg16_1 (
    .I(reg16_1_i), .A(subtractor_1_out), .DEC(decSC), .CLK(CLK), .LD(ldSC));  // open: Cout, Eout, SL, IL, SR, IR, INC, CL
  nor nor_1 (SC0, reg16_1_i[15], reg16_1_i[14], reg16_1_i[13], reg16_1_i[12], reg16_1_i[11], reg16_1_i[10], reg16_1_i[9], reg16_1_i[8], reg16_1_i[7], reg16_1_i[6], reg16_1_i[5], reg16_1_i[4], reg16_1_i[3], reg16_1_i[2], reg16_1_i[1], reg16_1_i[0], 1'b0);
  or or_1 (or_1_out, DAP[0], DAP[1]);
  and and_1 (and_1_out[0], or_1_out, DAP[15]);
  Adder #(.width(14)) adder_1 (.a(and_1_out), .b(DAP[15:2]), .out(adder_1_out));  // open: cin, cout
  Adder #(.width(14)) adder_2 (.a(adder_1_out), .b(DPB), .out(adder_2_out));  // open: cin, cout
  REG16 reg16_2 (
    .I(reg16_2_i), .DEC(decADR), .INC(incADR), .CL(clADR), .CLK(CLK));  // open: Cout, Eout, A, SL, IL, SR, IR, LD
  RAM #(.addrWidth(15), .dataWidth(14)) ram_1 (
    .addr(reg16_2_i[14:0]), .we(wrMEM), .oe(1'b1), .clk(CLK), .din(multiplexer_2_out), .dout(DPB));
  Multiplexer #(.enable("false"), .width(14)) multiplexer_2 (
    .in0(adder_1_out), .in1(adder_2_out), .out(multiplexer_2_out), .sel(S0));

  // Other names for the same wires on the sheet: Dout[13:0] = DPB
endmodule

module P_upravljacka (
  input  [2:0] Iin,
  input  CAP,
  input  SC0,
  input  N0
);

  wire T0, T1, T2, T3, T4;

  Decoder #(.enable("false"), .select(3)) decoder_1 (
    .out0(T0), .out1(T1), .out2(T2), .out3(T3), .out4(T4), .sel(Iin));  // open: out5, out6, out7
  // AND_Gate and_1 has open pins: in0=T0, in1=CAP, out=open
endmodule
