// Logisim project ORT2 K1N 2013 Logisim-evolution.circ as structural Verilog: 4 circuits, main circuit main
module main (
  input  in_1,
  input  in_2,
  input  [7:0] in_3,
  output out_4,
  output out_5,
  output out_6
);

  wire clock_1_out;

  Clock clock_1 (.out(clock_1_out));
  P p_1 (.CAP(in_1), .SBP(in_2), .CLK(clock_1_out), .DAP(in_3), .SPA(out_4), .SPB(out_5), .DPB(out_6));
endmodule

module P (
  input  CAP,
  input  SBP,
  input  CLK,
  input  [7:0] DAP,
  output SPA,
  output SPB,
  output DPB
);

  wire clCNT, clREG, decSC, incCNT, ldCNT, ldIncreasing, ldL, ldREG, ldSC, not_1_out, S0, SC0, srCNT;
  wire [1:0] Iin, Iout;

  P_upravljacka p_upravljacka_1 (
    .Iin(Iout), .SC0(SC0), .CAP(CAP), .SPB(SBP), .clCNT(clCNT), .clREG(clREG), .ldL(ldL), .ldSC(ldSC),
    .SPA(SPA), .ldREG(ldREG), .incCNT(incCNT), .ldIncreasing(ldIncreasing), .S0(S0), .Iout(Iin),
    .decSC(decSC), .ldCNT(ldCNT), .CPB(SPB), .srCNT(srCNT));
  REG2_CL_INC_LD reg2_cl_inc_ld_1 (
    .A1_0_e4900909(Iout), .INC(not_1_out), .CLK(CLK), .I1_0_431d2720(Iin), .LD(ldCNT));  // open: CL
  not not_1 (not_1_out, ldCNT);
  P_operaciona p_operaciona_1 (
    .S0(S0), .DAP(DAP), .ldREG(ldREG), .clCNT(clCNT), .srCNT(srCNT), .ldSC(ldSC), .CLK(CLK), .clREG(clREG),
    .decSC(decSC), .incCNT(incCNT), .ldL(ldL), .ldIncreasing(ldIncreasing), .DPB(DPB), .SC0(SC0));

  // Other names for the same wires on the sheet: CPB = SPB
endmodule

module P_operaciona (
  input  S0,
  input  [7:0] DAP,
  input  ldREG,
  input  clCNT,
  input  srCNT,
  input  ldSC,
  input  CLK,
  input  clREG,
  input  decSC,
  input  incCNT,
  input  ldL,
  input  ldIncreasing,
  output DPB,
  output SC0
);

  wire and_1_out, decreasing, increased, multiplexer_1_out, not_1_out, passesThreshold;
  wire [6:0] reg8_1_i;
  wire [7:0] L, multiplexer_2_out, reg8_2_i, reg8_cl_ld_1__7__0_2;

  REG8_CL_LD reg8_cl_ld_1 (._7__0_2(reg8_cl_ld_1__7__0_2), .LD(ldREG), .CL(clREG), .CLK(CLK), ._7__0(DAP));
  not not_1 (not_1_out, decreasing);
  D_Flip_Flop d_ff_1 (.D(multiplexer_1_out), .clk(CLK), .Q(increased));  // open: Qn, preset, reset
  Multiplexer #(.enable("false")) multiplexer_1 (
    .in0(increased), .in1(not_1_out), .out(multiplexer_1_out), .sel(ldIncreasing));
  Comparator #(.mode("unsigned")) comparator_1 (.a(reg8_cl_ld_1__7__0_2), .b(DAP), .gt(decreasing));  // open: eq, lt
  Comparator #(.mode("unsigned")) comparator_2 (.a(reg8_cl_ld_1__7__0_2), .b(L), .gt(passesThreshold));  // open: eq, lt
  REG8 reg8_1 (
    .I({DPB, reg8_1_i}), .CL(clCNT), .SL(srCNT), .IL(1'b0), .INC(and_1_out), .CLK(CLK));  // open: Cout, Eout, LD, SR, IR, DEC, A
  REG8_LD reg8_ld_1 (.A7_0_536de17e(L), .LD(ldL), .CLK(CLK), .I7_0_76b06db5(8'hf));
  and and_1 (and_1_out, passesThreshold, decreasing, increased, incCNT);
  Multiplexer #(.enable("false"), .width(8)) multiplexer_2 (
    .in0({8{1'b1}}), .in1(8'hf), .out(multiplexer_2_out), .sel(S0));
  REG8 reg8_2 (
    .I(reg8_2_i), .LD(ldSC), .DEC(decSC), .CLK(CLK), .A(multiplexer_2_out));  // open: Cout, Eout, CL, SL, IL, SR, IR, INC
  nor nor_1 (SC0, reg8_2_i[7], reg8_2_i[6], reg8_2_i[5], reg8_2_i[4], reg8_2_i[3], reg8_2_i[2], reg8_2_i[1], reg8_2_i[0]);
endmodule

module P_upravljacka (
  input  [1:0] Iin,
  input  SC0,
  input  CAP,
  input  SPB,
  output clCNT,
  output clREG,
  output ldL,
  output ldSC,
  output SPA,
  output ldREG,
  output incCNT,
  output ldIncreasing,
  output S0,
  output [1:0] Iout,
  output decSC,
  output ldCNT,
  output CPB,
  output srCNT
);

  wire and_4_out, nand_2_out, not_1_out, T2;

  Decoder #(.enable("false"), .select(2)) decoder_1 (.out0(clCNT), .out1(SPA), .out2(T2), .sel(Iin));  // open: out3
  nand nand_1 (Iout[0], SPA, CAP, SC0);
  or or_1 (ldCNT, Iout[0], nand_2_out);
  nand nand_2 (nand_2_out, T2, SPB, SC0);
  and and_1 (CPB, T2, SPB);
  and and_2 (incCNT, SPA, CAP);
  and and_3 (S0, incCNT, SC0);
  and and_4 (and_4_out, incCNT, not_1_out);
  not not_1 (not_1_out, SC0);
  or or_2 (decSC, and_4_out, CPB);
  or or_3 (ldSC, clCNT, S0);

  assign clREG = clCNT;
  assign Iout[1] = 1'b0;
  assign ldIncreasing = incCNT;
  assign ldL = clCNT;
  assign ldREG = incCNT;
  assign srCNT = CPB;

  // Other names for the same wires on the sheet: T0 = clCNT; T1 = SPA
endmodule
