// Logisim project Vezbe-1-2-compat.circ as structural Verilog: 4 circuits, main circuit main
module main (
  input  in_1,
  input  in_2,
  input  [8:0] in_3,
  output [2:0] out_4,
  output out_5,
  output out_6
);

  wire clock_1_out;

  Clock clock_1 (.out(clock_1_out));
  P p_1 (.clk(clock_1_out), .SBP(in_1), .CAP(in_2), .DAP(in_3), .DPB(out_4), .CPB(out_5), .SPA(out_6));
endmodule

module P (
  input  clk,
  input  SBP,
  input  CAP,
  input  [8:0] DAP,
  output [2:0] DPB,
  output CPB,
  output SPA
);

  wire not_1_out, p_operaciona_1_cntis0, p_operaciona_1_regeq, p_upravljacka_1_clout, p_upravljacka_1_deccnt,
       p_upravljacka_1_inccnt, p_upravljacka_1_incout, p_upravljacka_1_ldcnt, p_upravljacka_1_ldin,
       p_upravljacka_1_rstspa, p_upravljacka_1_srin, p_upravljacka_1_stspa;
  wire [1:0] p_upravljacka_1_outcnt0, reg2_cl_inc_ld_1_a1_0_e4900909;

  P_operaciona p_operaciona_1 (
    .DAP(DAP[7:0]), .ldIN(p_upravljacka_1_ldin), .ldCNT(p_upravljacka_1_ldcnt),
    .clOUT(p_upravljacka_1_clout), .srIN(p_upravljacka_1_srin), .decCNT(p_upravljacka_1_deccnt),
    .incOUT(p_upravljacka_1_incout), .clk(clk), .stSPA(p_upravljacka_1_stspa),
    .rstSPA(p_upravljacka_1_rstspa), .DPB(DPB), .cntIs0(p_operaciona_1_cntis0), .regEq(p_operaciona_1_regeq),
    .SPA(SPA));
  not not_1 (not_1_out, p_upravljacka_1_inccnt);
  REG2_CL_INC_LD reg2_cl_inc_ld_1 (
    .A1_0_e4900909(reg2_cl_inc_ld_1_a1_0_e4900909), .INC(p_upravljacka_1_inccnt), .CLK(clk),
    .I1_0_431d2720(p_upravljacka_1_outcnt0), .LD(not_1_out));  // open: CL
  P_upravljacka p_upravljacka_1 (
    .CAP(CAP), .cntIs0(p_operaciona_1_cntis0), .regEq(p_operaciona_1_regeq), .DAP8(DAP[8]), .SBP(SBP),
    .CNT0(reg2_cl_inc_ld_1_a1_0_e4900909[0]), .CNT1(reg2_cl_inc_ld_1_a1_0_e4900909[1]),
    .incCNT(p_upravljacka_1_inccnt), .outCNT1(p_upravljacka_1_outcnt0[1]),
    .outCNT0(p_upravljacka_1_outcnt0[0]), .ldIN(p_upravljacka_1_ldin), .ldCNT(p_upravljacka_1_ldcnt),
    .clOUT(p_upravljacka_1_clout), .rstSPA(p_upravljacka_1_rstspa), .stSPA(p_upravljacka_1_stspa),
    .srIN(p_upravljacka_1_srin), .decCNT(p_upravljacka_1_deccnt), .incOUT(p_upravljacka_1_incout), .CPB(CPB));
endmodule

module P_operaciona (
  input  [7:0] DAP,
  input  ldIN,
  input  ldCNT,
  input  clOUT,
  input  srIN,
  input  decCNT,
  input  incOUT,
  input  clk,
  input  stSPA,
  input  rstSPA,
  output [2:0] DPB,
  output cntIs0,
  output regEq,
  output SPA
);

  wire [7:0] reg8_1_i, reg8_2_i;
  wire [7:3] reg8_3_i;

  REG8 reg8_1 (
    .I(reg8_1_i), .LD(ldIN), .SR(srIN), .IR(1'b0), .CLK(clk), .A(DAP));  // open: Cout, Eout, CL, SL, IL, DEC, INC
  S_R_Flip_Flop s_r_ff_1 (.S(stSPA), .R(rstSPA), .clk(clk), .Q(SPA));  // open: reset, Qn, preset
  xnor xnor_1 (regEq, reg8_1_i[1], reg8_1_i[0]);
  REG8 reg8_2 (
    .I(reg8_2_i), .LD(ldCNT), .INC(decCNT), .CLK(clk), .A(8'h7));  // open: Cout, Eout, CL, SL, IL, SR, IR, DEC
  nor nor_1 (cntIs0, reg8_2_i[2], reg8_2_i[1], reg8_2_i[0]);
  REG8 reg8_3 (
    .I({reg8_3_i, DPB}), .CL(clOUT), .DEC(incOUT), .CLK(clk));  // open: Cout, Eout, LD, SL, IL, SR, IR, INC, A
endmodule

module P_upravljacka (
  input  CAP,
  input  cntIs0,
  input  regEq,
  input  DAP8,
  input  SBP,
  input  CNT0,
  input  CNT1,
  output incCNT,
  output outCNT1,
  output outCNT0,
  output ldIN,
  output ldCNT,
  output clOUT,
  output rstSPA,
  output stSPA,
  output srIN,
  output decCNT,
  output incOUT,
  output CPB
);

  wire and_1_out, and_2_out, and_3_out, and_4_out, and_5_out, and_6_out, decoder_1_out0, decoder_1_out3,
       xnor_1_out;

  xnor xnor_1 (xnor_1_out, regEq, DAP8);
  Decoder #(.select(2), .enable("false")) decoder_1 (
    .out0(decoder_1_out0), .out1(decCNT), .out2(incOUT), .out3(decoder_1_out3), .sel({CNT1, CNT0}));
  and and_1 (and_1_out, ~CNT0, ~CNT1, CAP);  // AND_Gate
  or or_1 (incCNT, and_1_out, and_2_out);
  and and_2 (and_2_out, CNT0, ~cntIs0, ~CNT1, xnor_1_out);  // AND_Gate
  and and_3 (and_3_out, CNT0, ~CNT1, cntIs0);  // AND_Gate
  and and_4 (and_4_out, ~SBP, CNT1, CNT0);  // AND_Gate
  and and_5 (and_5_out, ~cntIs0, ~xnor_1_out, CNT0, ~CNT1);  // AND_Gate
  and and_6 (and_6_out, CNT1, ~CNT0);  // AND_Gate
  and and_7 (clOUT, decoder_1_out0, CAP);
  and and_8 (stSPA, decoder_1_out0, ~CAP);  // AND_Gate
  and and_9 (CPB, decoder_1_out3, CNT1);
  or or_2 (outCNT1, and_3_out, and_4_out);
  or or_3 (outCNT0, and_3_out, and_4_out, and_5_out, and_6_out);

  assign ldCNT = clOUT;
  assign ldIN = clOUT;
  assign rstSPA = clOUT;
  assign srIN = decCNT;
endmodule
