// Logisim project PORT.circ as structural Verilog: 32 circuits, main circuit main
module main (
  input  [3:0] in_1,
  input  in_2
);

  wire sevensegmentinterface_1_a, sevensegmentinterface_1_b, sevensegmentinterface_1_c,
       sevensegmentinterface_1_d, sevensegmentinterface_1_e, sevensegmentinterface_1_f,
       sevensegmentinterface_1_g;

  SevenSegmentInterface sevensegmentinterface_1 (
    .x(in_1), .enable(in_2), .a(sevensegmentinterface_1_a), .b(sevensegmentinterface_1_b),
    .c(sevensegmentinterface_1_c), .d(sevensegmentinterface_1_d), .e(sevensegmentinterface_1_e),
    .f(sevensegmentinterface_1_f), .g(sevensegmentinterface_1_g));
  _7_Segment_Display #(.active("false")) u_7_segment_display_1 (
    .g(sevensegmentinterface_1_g), .f(sevensegmentinterface_1_f), .a(sevensegmentinterface_1_a),
    .b(sevensegmentinterface_1_b), .e(sevensegmentinterface_1_e), .d(sevensegmentinterface_1_d),
    .c(sevensegmentinterface_1_c), .dp(1'b1));
endmodule

module RisingEdgeRS (
  input  in1,
  input  clk,
  output out1
);

  wire and_1_out, not_1_out, s_r_ff_1_q, s_r_ff_2_qn;

  S_R_Flip_Flop s_r_ff_1 (.S(in1), .R(not_1_out), .clk(clk), .Q(s_r_ff_1_q));  // open: reset, Qn, preset
  not not_1 (not_1_out, in1);
  and and_1 (and_1_out, in1, s_r_ff_1_q);
  S_R_Flip_Flop s_r_ff_2 (.S(and_1_out), .R(not_1_out), .clk(clk), .Qn(s_r_ff_2_qn));  // open: Q, reset, preset
  and and_2 (out1, s_r_ff_1_q, s_r_ff_2_qn);
endmodule

module RisingEdgeT (
  input  in1,
  input  clk,
  output out1
);

  wire and_1_out, and_2_out, or_1_out, t_ff_1_q, t_ff_2_q, xor_1_out;

  and and_1 (and_1_out, t_ff_2_q, ~in1);  // AND_Gate
  or or_1 (or_1_out, and_1_out, and_2_out);
  and and_2 (and_2_out, t_ff_1_q, ~t_ff_2_q, in1);  // AND_Gate
  T_Flip_Flop t_ff_1 (.T(xor_1_out), .clk(clk), .Q(t_ff_1_q));  // open: Qn, reset, preset
  xor xor_1 (xor_1_out, in1, t_ff_1_q);
  T_Flip_Flop t_ff_2 (.T(or_1_out), .clk(clk), .Q(t_ff_2_q));  // open: Qn, reset, preset
  and and_3 (out1, t_ff_1_q, ~t_ff_2_q);  // AND_Gate
endmodule

module RisingEdgeD (
  input  in1,
  input  clk,
  output out1
);

  wire and_1_out, d_ff_1_q, d_ff_2_q;

  and and_1 (and_1_out, in1, d_ff_1_q);
  D_Flip_Flop d_ff_1 (.D(in1), .clk(clk), .Q(d_ff_1_q));  // open: Qn, preset, reset
  D_Flip_Flop d_ff_2 (.D(and_1_out), .clk(clk), .Q(d_ff_2_q));  // open: Qn, preset, reset
  and and_2 (out1, d_ff_1_q, ~d_ff_2_q);  // AND_Gate
endmodule

module RisingEdgeMealyD (
  input  x,
  input  clk,
  output out_3
);

  wire d_ff_1_qn;

  D_Flip_Flop d_ff_1 (.D(x), .clk(clk), .Qn(d_ff_1_qn));  // open: Q, preset, reset
  and and_1 (out_3, x, d_ff_1_qn);
endmodule

module MX2_4 (
  input  [3:0] i0,
  input  [3:0] i1,
  input  s0,
  output [3:0] a
);

  wire not_1_out;
  wire [3:0] and_1_out, and_2_out, bit_extender_1_out, bit_extender_2_out;

  not not_1 (not_1_out, s0);
  assign bit_extender_1_out = {{3{s0}}, s0};  // Bit_Extender bit_extender_1
  assign and_1_out = i0 & bit_extender_2_out;  // AND_Gate and_1, 4 bits wide
  assign and_2_out = i1 & bit_extender_1_out;  // AND_Gate and_2, 4 bits wide
  assign bit_extender_2_out = {{3{not_1_out}}, not_1_out};  // Bit_Extender bit_extender_2
  assign a = and_1_out | and_2_out;  // OR_Gate or_1, 4 bits wide
endmodule

module MX4_4 (
  input  [3:0] i0,
  input  [3:0] i1,
  input  [3:0] i2,
  input  [3:0] i3,
  input  s0,
  input  s1,
  output [3:0] a
);

  wire [3:0] mx2_4_1_a, mx2_4_2_a;

  MX2_4 mx2_4_1 (.i0(i0), .i1(i1), .s0(s0), .a(mx2_4_1_a));
  MX2_4 mx2_4_2 (.i0(i2), .i1(i3), .s0(s0), .a(mx2_4_2_a));
  MX2_4 mx2_4_3 (.i0(mx2_4_1_a), .i1(mx2_4_2_a), .s0(s1), .a(a));
endmodule

module DC2_1 (
  input  [1:0] in_1,
  output y0,
  output y1,
  output y2,
  output y3
);

  and and_1 (y0, ~in_1[0], ~in_1[1]);  // AND_Gate
  and and_2 (y1, in_1[0], ~in_1[1]);  // AND_Gate
  and and_3 (y2, ~in_1[0], in_1[1]);  // AND_Gate
  and and_4 (y3, in_1[0], in_1[1]);
endmodule

module DC3_1 (
  input  [2:0] x,
  output y0,
  output y1,
  output y2,
  output y3,
  output y4,
  output y5,
  output y6,
  output y7
);

  wire dc2_1_1_y0, dc2_1_1_y1, dc2_1_1_y2, dc2_1_1_y3;

  DC2_1 dc2_1_1 (.in_1(x[1:0]), .y0(dc2_1_1_y0), .y1(dc2_1_1_y1), .y2(dc2_1_1_y2), .y3(dc2_1_1_y3));
  and and_1 (y0, dc2_1_1_y0, ~x[2]);  // AND_Gate
  and and_2 (y1, dc2_1_1_y1, ~x[2]);  // AND_Gate
  and and_3 (y2, dc2_1_1_y2, ~x[2]);  // AND_Gate
  and and_4 (y3, dc2_1_1_y3, ~x[2]);  // AND_Gate
  and and_5 (y4, dc2_1_1_y0, x[2]);
  and and_6 (y5, dc2_1_1_y1, x[2]);
  and and_7 (y6, dc2_1_1_y2, x[2]);
  and and_8 (y7, dc2_1_1_y3, x[2]);
endmodule

module DC4_1 (
  input  [3:0] x,
  output y0,
  output y1,
  output y2,
  output y3,
  output y4,
  output y5,
  output y6,
  output y7,
  output y8,
  output y9,
  output y10,
  output y11,
  output y12,
  output y13,
  output y14,
  output y15
);

  wire dc3_1_1_y0, dc3_1_1_y1, dc3_1_1_y2, dc3_1_1_y3, dc3_1_1_y4, dc3_1_1_y5, dc3_1_1_y6, dc3_1_1_y7;

  DC3_1 dc3_1_1 (
    .x(x[2:0]), .y0(dc3_1_1_y0), .y1(dc3_1_1_y1), .y2(dc3_1_1_y2), .y3(dc3_1_1_y3), .y4(dc3_1_1_y4),
    .y5(dc3_1_1_y5), .y6(dc3_1_1_y6), .y7(dc3_1_1_y7));
  and and_1 (y0, dc3_1_1_y0, ~x[3]);  // AND_Gate
  and and_2 (y1, dc3_1_1_y1, ~x[3]);  // AND_Gate
  and and_3 (y2, dc3_1_1_y2, ~x[3]);  // AND_Gate
  and and_4 (y3, dc3_1_1_y3, ~x[3]);  // AND_Gate
  and and_5 (y4, dc3_1_1_y4, ~x[3]);  // AND_Gate
  and and_6 (y5, dc3_1_1_y5, ~x[3]);  // AND_Gate
  and and_7 (y6, dc3_1_1_y6, ~x[3]);  // AND_Gate
  and and_8 (y7, dc3_1_1_y7, ~x[3]);  // AND_Gate
  and and_9 (y8, dc3_1_1_y0, x[3]);
  and and_10 (y9, dc3_1_1_y1, x[3]);
  and and_11 (y10, dc3_1_1_y2, x[3]);
  and and_12 (y11, dc3_1_1_y3, x[3]);
  and and_13 (y12, dc3_1_1_y4, x[3]);
  and and_14 (y13, dc3_1_1_y5, x[3]);
  and and_15 (y14, dc3_1_1_y6, x[3]);
  and and_16 (y15, dc3_1_1_y7, x[3]);
endmodule

module CD4_1 (
  input  i0,
  input  i1,
  input  i2,
  input  i3,
  output a0,
  output a1,
  output w
);

  or or_1 (a0, i1, i3);
  or or_2 (a1, i2, i3);
  or or_3 (w, i0, i1, i2, i3);
endmodule

module CD8_1 (
  input  i0,
  input  i1,
  input  i2,
  input  i3,
  input  i4,
  input  i5,
  input  i6,
  input  i7,
  output a0,
  output a1,
  output a2,
  output w
);

  wire cd4_1_1_a0, cd4_1_1_a1, cd4_1_1_w, cd4_1_2_a0, cd4_1_2_a1;

  CD4_1 cd4_1_1 (.i0(i0), .i1(i1), .i2(i2), .i3(i3), .a0(cd4_1_1_a0), .a1(cd4_1_1_a1), .w(cd4_1_1_w));
  CD4_1 cd4_1_2 (.i0(i4), .i1(i5), .i2(i6), .i3(i7), .a0(cd4_1_2_a0), .a1(cd4_1_2_a1), .w(a2));
  or or_1 (a0, cd4_1_1_a0, cd4_1_2_a0);
  or or_2 (a1, cd4_1_1_a1, cd4_1_2_a1);
  or or_3 (w, cd4_1_1_w, a2);
endmodule

module DX2_4 (
  input  [3:0] i,
  input  s0,
  output [3:0] a0,
  output [3:0] a1
);

  wire not_1_out;
  wire [3:0] bit_extender_1_out, bit_extender_2_out;

  not not_1 (not_1_out, s0);
  assign bit_extender_1_out = {{3{s0}}, s0};  // Bit_Extender bit_extender_1
  assign a0 = i & bit_extender_2_out;  // AND_Gate and_1, 4 bits wide
  assign a1 = i & bit_extender_1_out;  // AND_Gate and_2, 4 bits wide
  assign bit_extender_2_out = {{3{not_1_out}}, not_1_out};  // Bit_Extender bit_extender_2
endmodule

module DX4_4 (
  input  [3:0] i,
  input  s1,
  input  s0,
  output [3:0] a0,
  output [3:0] a1,
  output [3:0] a2,
  output [3:0] a3
);

  wire [3:0] dx2_4_1_a0, dx2_4_1_a1;

  DX2_4 dx2_4_1 (.i(i), .s0(s1), .a0(dx2_4_1_a0), .a1(dx2_4_1_a1));
  DX2_4 dx2_4_2 (.i(dx2_4_1_a0), .s0(s0), .a0(a0), .a1(a1));
  DX2_4 dx2_4_3 (.i(dx2_4_1_a1), .s0(s0), .a0(a2), .a1(a3));
endmodule

module SevenSegmentInterface (
  input  [3:0] x,
  input  enable,
  output a,
  output b,
  output c,
  output d,
  output e,
  output f,
  output g
);

  wire dc4_1_1_y0, dc4_1_1_y1, dc4_1_1_y2, dc4_1_1_y3, dc4_1_1_y4, dc4_1_1_y5, dc4_1_1_y6, dc4_1_1_y7,
       dc4_1_1_y8, dc4_1_1_y9, not_1_out, not_2_out, or_1_out, or_2_out;

  DC4_1 dc4_1_1 (
    .x(x), .y0(dc4_1_1_y0), .y1(dc4_1_1_y1), .y2(dc4_1_1_y2), .y3(dc4_1_1_y3), .y4(dc4_1_1_y4),
    .y5(dc4_1_1_y5), .y6(dc4_1_1_y6), .y7(dc4_1_1_y7), .y8(dc4_1_1_y8), .y9(dc4_1_1_y9));  // open: y10, y11, y12, y13, y14, y15
  not not_1 (not_1_out, enable);
  or or_1 (or_1_out, not_1_out, not_2_out);
  or or_2 (or_2_out, dc4_1_1_y9, dc4_1_1_y8, dc4_1_1_y7, dc4_1_1_y6, dc4_1_1_y5, dc4_1_1_y4, dc4_1_1_y3, dc4_1_1_y2, dc4_1_1_y1, dc4_1_1_y0);
  not not_2 (not_2_out, or_2_out);
  or or_3 (a, dc4_1_1_y4, dc4_1_1_y1, or_1_out);
  or or_4 (b, dc4_1_1_y5, dc4_1_1_y6, or_1_out);
  or or_5 (c, dc4_1_1_y2, or_1_out);
  or or_6 (d, dc4_1_1_y1, dc4_1_1_y4, dc4_1_1_y7, or_1_out);
  or or_7 (e, dc4_1_1_y1, dc4_1_1_y3, dc4_1_1_y4, dc4_1_1_y5, dc4_1_1_y7, dc4_1_1_y9, or_1_out);
  or or_8 (f, dc4_1_1_y1, dc4_1_1_y2, dc4_1_1_y3, dc4_1_1_y7, or_1_out);
  or or_9 (g, dc4_1_1_y0, dc4_1_1_y1, dc4_1_1_y7, or_1_out);
endmodule

module REG1_RS (
  input  LD,
  input  Ii,
  input  SL,
  input  IL,
  input  SR,
  input  IR,
  input  INC,
  input  DEC,
  input  CL,
  input  clk,
  output Ai,
  output Aout,
  output Eout
);

  wire and_1_out, and_2_out, and_3_out, and_4_out, and_5_out, and_6_out, and_7_out, and_8_out, and_9_out,
       and_10_out, not_1_out, not_2_out, not_3_out, not_4_out, or_1_out, or_2_out;

  not not_1 (not_1_out, Ii);
  not not_2 (not_2_out, IL);
  not not_3 (not_3_out, IR);
  and and_1 (and_1_out, LD, Ii);
  and and_2 (and_2_out, LD, not_1_out);
  and and_3 (and_3_out, SL, IL);
  and and_4 (and_4_out, SL, not_2_out);
  and and_5 (and_5_out, SR, IR);
  and and_6 (and_6_out, SR, not_3_out);
  and and_7 (and_7_out, INC, not_4_out);
  and and_8 (and_8_out, INC, Ai);
  and and_9 (and_9_out, DEC, not_4_out);
  and and_10 (and_10_out, DEC, Ai);
  or or_1 (or_1_out, and_1_out, and_3_out, and_5_out, and_7_out, and_9_out);
  or or_2 (or_2_out, and_2_out, and_4_out, and_6_out, and_8_out, and_10_out, CL);
  S_R_Flip_Flop s_r_ff_1 (.S(or_1_out), .R(or_2_out), .clk(clk), .Q(Ai));  // open: reset, Qn, preset
  not not_4 (not_4_out, Ai);
  and and_11 (Aout, Ai, INC);
  and and_12 (Eout, not_4_out, DEC);
endmodule

module REG1_JK (
  input  LD,
  input  Ii,
  input  SL,
  input  IL,
  input  SR,
  input  IR,
  input  INC,
  input  DEC,
  input  CL,
  input  clk,
  output Ai,
  output Aout,
  output Eout
);

  wire and_1_out, and_2_out, and_3_out, and_4_out, and_5_out, and_6_out, not_1_out, not_2_out, not_3_out,
       or_1_out, or_2_out;

  not not_1 (not_1_out, Ii);
  not not_2 (not_2_out, IL);
  not not_3 (not_3_out, IR);
  and and_1 (and_1_out, LD, Ii);
  and and_2 (and_2_out, LD, not_1_out);
  and and_3 (and_3_out, SL, IL);
  and and_4 (and_4_out, SL, not_2_out);
  and and_5 (and_5_out, SR, IR);
  and and_6 (and_6_out, SR, not_3_out);
  or or_1 (or_1_out, and_1_out, and_3_out, and_5_out, INC, DEC);
  or or_2 (or_2_out, and_2_out, and_4_out, and_6_out, DEC, INC, CL);
  J_K_Flip_Flop j_k_ff_1 (.J(or_1_out), .K(or_2_out), .clk(clk), .Q(Ai));  // open: Qn, preset, reset
  and and_7 (Aout, Ai, INC);
  and and_8 (Eout, ~Ai, DEC);  // AND_Gate
endmodule

module REG1_T (
  input  LD,
  input  Ii,
  input  SL,
  input  IL,
  input  SR,
  input  IR,
  input  INC,
  input  DEC,
  input  CL,
  input  clk,
  output Ai,
  output Aout,
  output Eout
);

  wire and_1_out, and_2_out, and_3_out, and_4_out, and_5_out, and_6_out, and_7_out, or_1_out;

  and and_1 (and_1_out, Ai, CL);
  and and_2 (and_2_out, LD, ~Ai, Ii);  // AND_Gate
  and and_3 (and_3_out, LD, Ai, ~Ii);  // AND_Gate
  and and_4 (and_4_out, SL, ~Ai, IL);  // AND_Gate
  and and_5 (and_5_out, SL, Ai, ~IL);  // AND_Gate
  and and_6 (and_6_out, SR, ~Ai, IR);  // AND_Gate
  and and_7 (and_7_out, SR, Ai, ~IR);  // AND_Gate
  T_Flip_Flop t_ff_1 (.T(or_1_out), .clk(clk), .Q(Ai));  // open: Qn, reset, preset
  or or_1 (or_1_out, and_2_out, and_3_out, and_4_out, and_5_out, and_6_out, and_7_out, INC, DEC, and_1_out);
  and and_8 (Aout, Ai, INC);
  and and_9 (Eout, ~Ai, DEC);  // AND_Gate
endmodule

module REG1_D (
  input  LD,
  input  Ii,
  input  SL,
  input  IL,
  input  SR,
  input  IR,
  input  INC,
  input  DEC,
  input  CL,
  input  clk,
  output Ai,
  output Aout,
  output Eout
);

  wire and_1_out, and_2_out, and_3_out, and_4_out, and_5_out, and_6_out, or_1_out;

  and and_1 (and_1_out, LD, Ii);
  and and_2 (and_2_out, SL, IL);
  and and_3 (and_3_out, SR, IR);
  and and_4 (and_4_out, INC, ~Ai);  // AND_Gate
  and and_5 (and_5_out, DEC, ~Ai);  // AND_Gate
  or or_1 (or_1_out, and_1_out, and_2_out, and_3_out, and_4_out, and_5_out, and_6_out);
  and and_6 (and_6_out, Ai, ~LD, ~SL, ~SR, ~INC, ~DEC, ~CL);  // AND_Gate
  D_Flip_Flop d_ff_1 (.D(or_1_out), .clk(clk), .Q(Ai));  // open: Qn, preset, reset
  and and_7 (Aout, Ai, INC);
  and and_8 (Eout, DEC, ~Ai);  // AND_Gate
endmodule

module REG4_RS (
  input  LD,
  input  [3:0] I,
  input  SL,
  input  SR,
  input  IL,
  input  IR,
  input  INC,
  input  DEC,
  input  CL,
  input  clk,
  output Aout,
  output Eout,
  output [3:0] A
);

  wire reg1_rs_1_aout, reg1_rs_1_eout, reg1_rs_2_aout, reg1_rs_2_eout, reg1_rs_3_aout, reg1_rs_3_eout;

  REG1_RS reg1_rs_1 (
    .LD(LD), .Ii(I[0]), .SL(SL), .IL(IL), .SR(SR), .IR(A[1]), .INC(INC), .DEC(DEC), .CL(CL), .clk(clk),
    .Ai(A[0]), .Aout(reg1_rs_1_aout), .Eout(reg1_rs_1_eout));
  REG1_RS reg1_rs_2 (
    .LD(LD), .Ii(I[1]), .SL(SL), .IL(A[0]), .SR(SR), .IR(A[2]), .INC(reg1_rs_1_aout), .DEC(reg1_rs_1_eout),
    .CL(CL), .clk(clk), .Ai(A[1]), .Aout(reg1_rs_2_aout), .Eout(reg1_rs_2_eout));
  REG1_RS reg1_rs_3 (
    .LD(LD), .Ii(I[2]), .SL(SL), .IL(A[1]), .SR(SR), .IR(A[3]), .INC(reg1_rs_2_aout), .DEC(reg1_rs_2_eout),
    .CL(CL), .clk(clk), .Ai(A[2]), .Aout(reg1_rs_3_aout), .Eout(reg1_rs_3_eout));
  REG1_RS reg1_rs_4 (
    .LD(LD), .Ii(I[3]), .SL(SL), .IL(A[2]), .SR(SR), .IR(IR), .INC(reg1_rs_3_aout), .DEC(reg1_rs_3_eout),
    .CL(CL), .clk(clk), .Ai(A[3]), .Aout(Aout), .Eout(Eout));
endmodule

module RSFF (
  input  S,
  input  R,
  output notQ,
  output Q
);

  nor nor_1 (notQ, S, Q);
  nor nor_2 (Q, notQ, R);
endmodule

module ADD1 (
  input  A,
  input  B,
  input  Cin,
  output F,
  output Cout
);

  wire and_1_out, and_2_out, and_3_out, and_4_out, and_5_out, and_6_out, and_7_out;

  and and_1 (and_1_out, ~A, ~B, Cin);  // AND_Gate
  and and_2 (and_2_out, ~A, B, ~Cin);  // AND_Gate
  and and_3 (and_3_out, A, B, Cin);
  and and_4 (and_4_out, A, ~B, ~Cin);  // AND_Gate
  and and_5 (and_5_out, A, B);
  and and_6 (and_6_out, Cin, B);
  and and_7 (and_7_out, A, Cin);
  or or_1 (F, and_1_out, and_2_out, and_3_out, and_4_out);
  or or_2 (Cout, and_5_out, and_6_out, and_7_out);
endmodule

module ADD4 (
  input  [3:0] A,
  input  [3:0] B,
  output Cout,
  output [3:0] F
);

  wire add1_1_cout, add1_2_cout, add1_3_cout;

  ADD1 add1_1 (.A(A[0]), .B(B[0]), .Cin(1'b0), .F(F[0]), .Cout(add1_1_cout));
  ADD1 add1_2 (.A(A[1]), .B(B[1]), .Cin(add1_1_cout), .F(F[1]), .Cout(add1_2_cout));
  ADD1 add1_3 (.A(A[2]), .B(B[2]), .Cin(add1_2_cout), .F(F[2]), .Cout(add1_3_cout));
  ADD1 add1_4 (.A(A[3]), .B(B[3]), .Cin(add1_3_cout), .F(F[3]), .Cout(Cout));
endmodule

module CMP1 (
  input  A,
  input  B,
  input  Gprev,
  input  Lprev,
  output G,
  output L,
  output E
);

  wire and_1_out, and_2_out, and_3_out, and_4_out, xnor_1_out;

  xnor xnor_1 (xnor_1_out, A, B);
  and and_1 (and_1_out, A, ~B);  // AND_Gate
  or or_1 (G, and_1_out, and_2_out);
  and and_2 (and_2_out, xnor_1_out, Gprev);
  and and_3 (and_3_out, Lprev, xnor_1_out);
  or or_2 (L, and_3_out, and_4_out);
  and and_4 (and_4_out, ~A, B);  // AND_Gate
  and and_5 (E, xnor_1_out, ~Gprev, ~Lprev);  // AND_Gate
endmodule

module CMP4 (
  input  [3:0] A,
  input  [3:0] B,
  output G,
  output L,
  output E
);

  wire cmp1_1_g, cmp1_1_l, cmp1_2_g, cmp1_2_l, cmp1_3_g, cmp1_3_l;

  CMP1 cmp1_1 (.A(A[0]), .B(B[0]), .Gprev(1'b0), .Lprev(1'b0), .G(cmp1_1_g), .L(cmp1_1_l));  // open: E
  CMP1 cmp1_2 (.A(A[1]), .B(B[1]), .Gprev(cmp1_1_g), .Lprev(cmp1_1_l), .G(cmp1_2_g), .L(cmp1_2_l));  // open: E
  CMP1 cmp1_3 (.A(A[2]), .B(B[2]), .Gprev(cmp1_2_g), .Lprev(cmp1_2_l), .G(cmp1_3_g), .L(cmp1_3_l));  // open: E
  CMP1 cmp1_4 (.A(A[3]), .B(B[3]), .Gprev(cmp1_3_g), .Lprev(cmp1_3_l), .G(G), .L(L), .E(E));
endmodule

module ADD1_CG (
  input  A,
  input  B,
  input  Cin,
  output F,
  output Cout,
  output P,
  output G
);

  wire and_1_out, and_2_out, and_3_out, and_4_out, and_5_out, and_6_out, and_7_out;

  and and_1 (and_1_out, ~A, ~B, Cin);  // AND_Gate
  and and_2 (and_2_out, ~A, B, ~Cin);  // AND_Gate
  and and_3 (and_3_out, A, B, Cin);
  and and_4 (and_4_out, A, ~B, ~Cin);  // AND_Gate
  and and_5 (and_5_out, A, B);
  and and_6 (and_6_out, Cin, B);
  and and_7 (and_7_out, A, Cin);
  xor xor_1 (P, A, B);
  and and_8 (G, A, B);
  or or_1 (F, and_1_out, and_2_out, and_3_out, and_4_out);
  or or_2 (Cout, and_5_out, and_6_out, and_7_out);
endmodule

module ADD4_CG (
  input  [3:0] A,
  input  [3:0] B,
  input  Cin,
  output [3:0] F,
  output Cout
);

  wire add1_cg_1_cout, add1_cg_1_g, add1_cg_1_p, add1_cg_2_g, add1_cg_2_p, add1_cg_3_g, add1_cg_3_p,
       add1_cg_4_g, add1_cg_4_p, cg4_1_c1, cg4_1_c2, cg4_1_c3;

  ADD1_CG add1_cg_1 (.A(A[0]), .B(B[0]), .Cin(Cin), .F(F[0]), .Cout(add1_cg_1_cout), .P(add1_cg_1_p), .G(add1_cg_1_g));
  ADD1_CG add1_cg_2 (.A(A[1]), .B(B[1]), .Cin(cg4_1_c1), .F(F[1]), .P(add1_cg_2_p), .G(add1_cg_2_g));  // open: Cout
  ADD1_CG add1_cg_3 (.A(A[2]), .B(B[2]), .Cin(cg4_1_c2), .F(F[2]), .P(add1_cg_3_p), .G(add1_cg_3_g));  // open: Cout
  ADD1_CG add1_cg_4 (.A(A[3]), .B(B[3]), .Cin(cg4_1_c3), .F(F[3]), .P(add1_cg_4_p), .G(add1_cg_4_g));  // open: Cout
  CG4 cg4_1 (
    .C0(add1_cg_1_cout), .P0(add1_cg_1_p), .G0(add1_cg_1_g), .P1(add1_cg_2_p), .G1(add1_cg_2_g),
    .P2(add1_cg_3_p), .G2(add1_cg_3_g), .P3(add1_cg_4_p), .G3(add1_cg_4_g), .C1(cg4_1_c1), .C2(cg4_1_c2),
    .C3(cg4_1_c3), .C4(Cout));
endmodule

module CG4 (
  input  C0,
  input  P0,
  input  G0,
  input  P1,
  input  G1,
  input  P2,
  input  G2,
  input  P3,
  input  G3,
  output C1,
  output C2,
  output C3,
  output C4
);

  wire and_1_out, and_2_out, and_3_out, and_4_out, and_5_out, and_6_out, and_7_out, and_8_out, and_9_out,
       and_10_out;

  and and_1 (and_1_out, C0, P0, P1);
  and and_2 (and_2_out, G0, P1);
  and and_3 (and_3_out, C0, P0, P1, P2);
  and and_4 (and_4_out, G0, P1, P2);
  and and_5 (and_5_out, G1, P2);
  and and_6 (and_6_out, C0, P0, P1, P2, P3);
  and and_7 (and_7_out, G0, P1, P2, P3);
  and and_8 (and_8_out, G1, P2, P3);
  and and_9 (and_9_out, G2, P3);
  and and_10 (and_10_out, C0, P0);
  or or_1 (C1, and_10_out, G0);
  or or_2 (C2, and_1_out, and_2_out, G1);
  or or_3 (C3, and_3_out, and_4_out, and_5_out, G2);
  or or_4 (C4, and_6_out, and_7_out, and_8_out, and_9_out, G3);
endmodule

module SH4 (
  input  [3:0] a,
  input  [2:0] sh,
  output [3:0] f
);

  wire and_2_out, and_3_out, and_4_out, and_5_out, and_6_out, and_7_out, and_8_out, and_9_out, and_10_out,
       dc3_1_1_y0, dc3_1_1_y1, dc3_1_1_y2, dc3_1_1_y3;

  DC3_1 dc3_1_1 (.x(sh), .y0(dc3_1_1_y0), .y1(dc3_1_1_y1), .y2(dc3_1_1_y2), .y3(dc3_1_1_y3));  // open: y4, y5, y6, y7
  and and_1 (f[0], a[0], dc3_1_1_y0);
  and and_2 (and_2_out, a[1], dc3_1_1_y0);
  and and_3 (and_3_out, a[0], dc3_1_1_y1);
  and and_4 (and_4_out, a[2], dc3_1_1_y0);
  and and_5 (and_5_out, a[1], dc3_1_1_y1);
  and and_6 (and_6_out, a[0], dc3_1_1_y2);
  and and_7 (and_7_out, a[3], dc3_1_1_y0);
  and and_8 (and_8_out, a[2], dc3_1_1_y1);
  and and_9 (and_9_out, a[1], dc3_1_1_y2);
  and and_10 (and_10_out, a[0], dc3_1_1_y3);
  or or_1 (f[1], and_2_out, and_3_out);
  or or_2 (f[2], and_4_out, and_5_out, and_6_out);
  or or_3 (f[3], and_7_out, and_8_out, and_9_out, and_10_out);
endmodule

module MEM1x4 (
  input  WR_RD,
  input  CS,
  input  [3:0] I,
  input  clk,
  output [3:0] A
);

  wire and_1_out, not_1_out;
  wire [3:0] bit_extender_1_out, bit_extender_2_out, reg4_rs_1_a;

  not not_1 (not_1_out, WR_RD);
  and and_1 (and_1_out, WR_RD, CS);
  assign bit_extender_1_out = {{3{not_1_out}}, not_1_out};  // Bit_Extender bit_extender_1
  assign bit_extender_2_out = {{3{CS}}, CS};  // Bit_Extender bit_extender_2
  REG4_RS reg4_rs_1 (
    .LD(and_1_out), .I(I), .clk(clk), .A(reg4_rs_1_a));  // open: SL, SR, IL, IR, INC, DEC, CL, Aout, Eout
  assign A = bit_extender_1_out & bit_extender_2_out & reg4_rs_1_a;  // AND_Gate and_2, 4 bits wide
endmodule

module MEM2x4 (
  input  WR_RD,
  input  CS,
  input  [3:0] I,
  input  clk,
  input  adr,
  output [3:0] A
);

  wire decoder_1_out0, decoder_1_out1;
  wire [3:0] mem1x4_1_a, mem1x4_2_a;

  Decoder decoder_1 (.out0(decoder_1_out0), .out1(decoder_1_out1), .sel(adr), .en(CS));
  MEM1x4 mem1x4_1 (.WR_RD(WR_RD), .CS(decoder_1_out0), .I(I), .clk(clk), .A(mem1x4_1_a));
  assign A = mem1x4_1_a | mem1x4_2_a;  // OR_Gate or_1, 4 bits wide
  MEM1x4 mem1x4_2 (.WR_RD(WR_RD), .CS(decoder_1_out1), .I(I), .clk(clk), .A(mem1x4_2_a));
endmodule

module MEM2x8 (
  input  WR_RD,
  input  CS,
  input  [7:0] I,
  input  clk,
  input  adr,
  output [7:0] A
);

  MEM2x4 mem2x4_1 (.WR_RD(WR_RD), .CS(CS), .I(I[3:0]), .clk(clk), .adr(adr), .A(A[3:0]));
  MEM2x4 mem2x4_2 (.WR_RD(WR_RD), .CS(CS), .I(I[7:4]), .clk(clk), .adr(adr), .A(A[7:4]));
endmodule
