// Logisim project dz1.circ as structural Verilog: 1 circuit, main circuit dz1
module dz1 (
  input  [3:0] in_1
);

  wire and_1_out, and_2_out, and_3_out, and_4_out, and_5_out, and_6_out, and_7_out, and_8_out, and_9_out,
       and_10_out, and_11_out, and_12_out, and_13_out, and_14_out, and_15_out, and_16_out, and_17_out,
       and_18_out, and_19_out, and_20_out, not_1_out, not_2_out, not_3_out, not_4_out, or_1_out, or_2_out,
       or_3_out, or_4_out, or_5_out, or_6_out, or_7_out;

  not not_1 (not_1_out, in_1[0]);
  not not_2 (not_2_out, in_1[1]);
  not not_3 (not_3_out, in_1[2]);
  not not_4 (not_4_out, in_1[3]);
  and and_1 (and_1_out, not_4_out, in_1[2], not_2_out, not_1_out);
  and and_2 (and_2_out, not_4_out, not_3_out, not_2_out, in_1[0]);
  or or_1 (or_1_out, and_1_out, and_2_out);
  and and_3 (and_3_out, in_1[3], in_1[2]);
  and and_4 (and_4_out, in_1[3], in_1[1]);
  and and_5 (and_5_out, not_4_out, not_2_out, in_1[0]);
  or or_2 (or_2_out, and_3_out, and_4_out, and_5_out, and_6_out);
  and and_6 (and_6_out, in_1[2], in_1[1], not_1_out);
  and and_7 (and_7_out, not_4_out, not_3_out, not_2_out, in_1[0]);
  and and_8 (and_8_out, not_3_out, in_1[1], not_1_out);
  or or_3 (or_3_out, and_7_out, and_8_out, and_9_out, and_10_out);
  and and_9 (and_9_out, in_1[3], in_1[2]);
  and and_10 (and_10_out, in_1[3], in_1[1]);
  and and_11 (and_11_out, not_4_out, in_1[2], not_2_out, not_1_out);
  _7_Segment_Display #(.active("false")) u_7_segment_display_1 (
    .g(or_7_out), .f(or_6_out), .a(or_1_out), .b(or_2_out), .e(or_5_out), .d(or_4_out), .c(or_3_out),
    .dp(1'b1));
  and and_12 (and_12_out, not_4_out, not_3_out, not_2_out, in_1[0]);
  and and_13 (and_13_out, not_4_out, in_1[2], in_1[1], in_1[0]);
  or or_4 (or_4_out, and_11_out, and_12_out, and_13_out);
  and and_14 (and_14_out, not_4_out, in_1[2], not_2_out);
  and and_15 (and_15_out, not_4_out, in_1[1], in_1[0]);
  and and_16 (and_16_out, in_1[3], not_3_out, not_2_out, in_1[0]);
  or or_5 (or_5_out, and_14_out, and_15_out, and_16_out);
  and and_17 (and_17_out, not_4_out, not_3_out, in_1[1]);
  and and_18 (and_18_out, not_4_out, in_1[1], in_1[0]);
  or or_6 (or_6_out, and_18_out, and_17_out);
  and and_19 (and_19_out, not_4_out, not_3_out, not_2_out);
  or or_7 (or_7_out, and_19_out, and_20_out);
  and and_20 (and_20_out, not_4_out, in_1[2], in_1[1], in_1[0]);
endmodule
