// Logisim project dz2.circ as structural Verilog: 2 circuits, main circuit dz2
module PRandom07 (
  input  rst,
  input  nxt,
  input  clk,
  output z2,
  output z1,
  output z0
);

  wire and_1_out, and_2_out, and_3_out, and_4_out, and_5_out, and_6_out, and_7_out, and_8_out, and_9_out,
       and_10_out, and_11_out, and_12_out, and_13_out, and_14_out, and_15_out, and_16_out, and_17_out,
       not_1_out, not_2_out, or_4_out, or_5_out, or_6_out, t_ff_1_q, t_ff_1_qn, t_ff_2_q, t_ff_2_qn,
       t_ff_3_q, t_ff_3_qn;

  not not_1 (not_1_out, rst);
  not not_2 (not_2_out, nxt);
  and and_1 (and_1_out, not_1_out, not_2_out, t_ff_1_q);
  and and_2 (and_2_out, not_1_out, nxt, t_ff_1_q, t_ff_3_qn);
  and and_3 (and_3_out, not_1_out, nxt, t_ff_1_qn, t_ff_2_q);
  or or_1 (z2, and_1_out, and_2_out, and_3_out, and_4_out);
  and and_4 (and_4_out, rst, nxt, t_ff_1_q);
  and and_5 (and_5_out, not_1_out, not_2_out, t_ff_2_q);
  and and_6 (and_6_out, not_1_out, nxt, t_ff_1_q, t_ff_2_qn);
  and and_7 (and_7_out, not_1_out, nxt, t_ff_2_qn, t_ff_3_qn);
  or or_2 (z1, and_5_out, and_2_out, and_6_out, and_7_out, and_8_out);
  and and_8 (and_8_out, rst, nxt, t_ff_2_q);
  and and_9 (and_9_out, not_1_out, not_2_out, t_ff_3_q);
  and and_10 (and_10_out, not_1_out, t_ff_1_q, t_ff_3_q);
  and and_11 (and_11_out, not_1_out, nxt, t_ff_2_q, t_ff_3_qn);
  or or_3 (z0, and_9_out, and_10_out, and_11_out, and_12_out);
  and and_12 (and_12_out, rst, nxt, t_ff_3_q);
  and and_13 (and_13_out, not_1_out, nxt, t_ff_1_q, t_ff_3_q);
  and and_14 (and_14_out, rst, not_2_out, t_ff_1_q);
  or or_4 (or_4_out, and_13_out, and_3_out, and_14_out);
  and and_15 (and_15_out, rst, not_2_out, t_ff_2_q);
  and and_16 (and_16_out, not_1_out, nxt, t_ff_1_qn, t_ff_3_q);
  or or_5 (or_5_out, and_7_out, and_13_out, and_3_out, and_15_out);
  and and_17 (and_17_out, rst, not_2_out, t_ff_3_q);
  or or_6 (or_6_out, and_16_out, and_11_out, and_17_out);
  T_Flip_Flop t_ff_1 (.T(or_4_out), .clk(clk), .Q(t_ff_1_q), .Qn(t_ff_1_qn));  // open: reset, preset
  T_Flip_Flop t_ff_2 (.T(or_5_out), .clk(clk), .Q(t_ff_2_q), .Qn(t_ff_2_qn));  // open: reset, preset
  T_Flip_Flop t_ff_3 (.T(or_6_out), .clk(clk), .Q(t_ff_3_q), .Qn(t_ff_3_qn));  // open: reset, preset
endmodule

module dz2 (
);

  wire and_1_out, btn0_out, btn1_out, clock_1_out, or_1_out, or_2_out, risingedge_1_out1, risingedge_2_out1;
  wire [2:0] prandom07_1_z0;

  Button btn0 (.out(btn0_out));
  Button btn1 (.out(btn1_out));
  Clock clock_1 (.out(clock_1_out));
  and and_1 (and_1_out, btn1_out, btn0_out);
  RisingEdge risingedge_1 (.in1(btn0_out), .clk(clock_1_out), .out1(risingedge_1_out1));
  RisingEdge risingedge_2 (.in1(btn1_out), .clk(clock_1_out), .out1(risingedge_2_out1));
  or or_1 (or_1_out, and_1_out, risingedge_1_out1);
  or or_2 (or_2_out, and_1_out, risingedge_2_out1);
  PRandom07 prandom07_1 (
    .rst(or_1_out), .nxt(or_2_out), .clk(clock_1_out), .z2(prandom07_1_z0[2]), .z1(prandom07_1_z0[1]),
    .z0(prandom07_1_z0[0]));
  _7_Segment_Display u_7_segment_display_1 ();  // open: g, f, a, b, e, d, c, dp
  // BCD_to_7_Segment_decoder bcd_to_7_segment_decoder_1: pin names not known
endmodule
