// Logisim project dz3.circ as structural Verilog: 1 circuit, main circuit dz3
module dz3 (
  input  [2:0] sw2_0,
  input  sw3,
  input  sw4,
  input  sw5,
  input  sw6,
  input  sw7,
  input  [1:0] sw8_9
);

  wire btn0_out, btn1_out, btn2_out, clock_1_out, comparator_1_eq, n7_segment_display_1_p1,
       n7_segment_display_2_p1, n7_segment_display_3_p1, priority_encoder_1_gs, risingedge_1_out1, xnor_1_out;
  wire [1:0] priority_encoder_1_out;
  wire [2:0] prandom07_1_z0;
  wire [6:0] adder_1_out, adder_2_out, adder_3_out, adder_4_out, multiplexer_1_out, multiplexer_2_out,
       multiplexer_3_out, multiplexer_4_out, multiplexer_5_out;

  Button btn0 (.out(btn0_out));
  Button btn1 (.out(btn1_out));
  Clock clock_1 (.out(clock_1_out));
  Button btn2 (.out(btn2_out));
  Multiplexer #(.enable("false"), .select(2), .width(7)) multiplexer_1 (
    .in0({7{1'b0}}), .in1(7'b0000101), .in2(7'b0001010), .in3(7'b0001111), .out(multiplexer_1_out),
    .sel(sw8_9));
  Priority_Encoder #(.select(2)) priority_encoder_1 (
    .in0(sw4), .in1(sw5), .in2(sw6), .in3(sw7), .out(priority_encoder_1_out), .gs(priority_encoder_1_gs));  // open: en_out, en_in
  Adder #(.width(7)) adder_1 (.a(multiplexer_2_out), .b(multiplexer_2_out), .out(adder_1_out));  // open: cin, cout
  Comparator #(.width(3)) comparator_1 (.a(prandom07_1_z0), .b(sw2_0), .eq(comparator_1_eq));  // open: gt, lt
  xnor xnor_1 (xnor_1_out, sw3, prandom07_1_z0[0]);
  Multiplexer #(.select(2), .width(7)) multiplexer_2 (
    .in0(7'b0000001), .in1(7'b0000010), .in2(7'b0000101), .in3(7'b0001010), .out(multiplexer_2_out),
    .sel(priority_encoder_1_out), .en(priority_encoder_1_gs));
  Adder #(.width(7)) adder_2 (.a(adder_1_out), .b(adder_1_out), .out(adder_2_out));  // open: cin, cout
  RisingEdge risingedge_1 (.in1(btn1_out), .clk(clock_1_out), .out1(risingedge_1_out1));
  Multiplexer #(.enable("false"), .width(7)) multiplexer_3 (
    .in0({7{1'b0}}), .in1(adder_3_out), .out(multiplexer_3_out), .sel(comparator_1_eq));
  Multiplexer #(.enable("false"), .width(7)) multiplexer_4 (
    .in0({7{1'b0}}), .in1(adder_1_out), .out(multiplexer_4_out), .sel(xnor_1_out));
  Adder #(.width(7)) adder_3 (.a(adder_2_out), .b(adder_2_out), .out(adder_3_out));  // open: cin, cout
  Multiplexer #(.enable("false"), .width(7)) multiplexer_5 (
    .in0(multiplexer_4_out), .in1(multiplexer_3_out), .out(multiplexer_5_out), .sel(btn2_out));
  Adder #(.width(7)) adder_4 (.a(multiplexer_5_out), .b(multiplexer_1_out), .out(adder_4_out));  // open: cin, cout
  // _7_Segment_Display 7_segment_display_1: pin names not known; wires that end beside it: n7_segment_display_1_p1, n7_segment_display_1_p1
  // BCD_to_7_Segment_decoder bcd_to_7_segment_decoder_1: pin names not known
  PRandom07 prandom07_1 (
    .rst(btn0_out), .nxt(risingedge_1_out1), .clk(clock_1_out), .z2(prandom07_1_z0[2]),
    .z1(prandom07_1_z0[1]), .z0(prandom07_1_z0[0]));
  // _7_Segment_Display 7_segment_display_2: pin names not known; wires that end beside it: n7_segment_display_2_p1, n7_segment_display_2_p1
  // BCD_to_7_Segment_decoder bcd_to_7_segment_decoder_2: pin names not known
  // Binairy_to_BCD_converter #(.binvalue(7)) binairy_to_bcd_converter_1: pin names not known; wires that end beside it: adder_4_out
  // _7_Segment_Display 7_segment_display_3: pin names not known; wires that end beside it: n7_segment_display_3_p1, n7_segment_display_3_p1
  // BCD_to_7_Segment_decoder bcd_to_7_segment_decoder_3: pin names not known
endmodule
