// Logisim project dz4.circ as structural Verilog: 4 circuits, main circuit dz4
module dz4 (
  input  sw0,
  input  sw1,
  input  sw3,
  input  sw4,
  input  sw5,
  input  sw6,
  input  sw7,
  input  sw8,
  input  sw9,
  output [7:0] LED
);

  wire and_1_out, and_2_out, and_3_out, and_4_out, and_5_out, btn0_out, btn1_out, clock_1_out,
       comparator_1_eq, n7_segment_display_1_p1, n7_segment_display_2_p1, n7_segment_display_3_p1, not_1_out,
       not_2_out, or_1_out, or_2_out, prandom07_2_z2, priority_encoder_1_gs, risingedge_1_out1,
       risingedge_2_out1, risingedge_3_out1, xnor_1_out;
  wire [1:0] priority_encoder_1_out;
  wire [4:0] prandom07_2_z0;
  wire [7:0] adder_1_out, adder_2_out, adder_3_out, adder_4_out, adder_5_out, chips_1_chipsy,
       multiplexer_1_out, multiplexer_2_out, multiplexer_3_out;

  Button btn0 (.out(btn0_out));
  Button btn1 (.out(btn1_out));
  Clock clock_1 (.out(clock_1_out));
  xnor xnor_1 (xnor_1_out, prandom07_2_z0[0], sw3);
  Priority_Encoder #(.select(2)) priority_encoder_1 (
    .in0(sw4), .in1(sw5), .in2(sw6), .in3(sw7), .out(priority_encoder_1_out), .gs(priority_encoder_1_gs));  // open: en_out, en_in
  Multiplexer #(.select(2), .width(8)) multiplexer_1 (
    .in0(8'h1), .in1(8'h2), .in2(8'h4), .in3(8'h6), .out(multiplexer_1_out), .sel(priority_encoder_1_out),
    .en(priority_encoder_1_gs));
  not not_1 (not_1_out, prandom07_2_z0[4]);
  not not_2 (not_2_out, prandom07_2_z0[3]);
  Multiplexer #(.width(8)) multiplexer_2 (
    .in0({8{1'b0}}), .in1(adder_1_out), .out(multiplexer_2_out), .sel(xnor_1_out), .en(sw9));
  Adder adder_1 (.a(multiplexer_1_out), .b(multiplexer_1_out), .out(adder_1_out));  // open: cin, cout
  RisingEdge risingedge_1 (.in1(btn1_out), .clk(clock_1_out), .out1(risingedge_1_out1));
  and and_1 (and_1_out, risingedge_1_out1, not_1_out, not_2_out, prandom07_2_z0[2]);
  RisingEdge risingedge_2 (.in1(sw0), .clk(clock_1_out), .out1(risingedge_2_out1));
  RisingEdge risingedge_3 (.in1(sw1), .clk(clock_1_out), .out1(risingedge_3_out1));
  Adder adder_2 (.a(adder_1_out), .b(adder_1_out), .out(adder_2_out));  // open: cin, cout
  Adder adder_3 (.a(adder_2_out), .b(adder_2_out), .out(adder_3_out));  // open: cin, cout
  Adder adder_4 (.a(adder_3_out), .b(adder_3_out), .out(adder_4_out));  // open: cin, cout
  and and_2 (and_2_out, sw8, comparator_1_eq);
  Adder adder_5 (.a(adder_4_out), .b(adder_4_out), .out(adder_5_out));  // open: cin, cout
  PRandom07 prandom07_1 (
    .rst(btn0_out), .nxt(risingedge_1_out1), .clk(clock_1_out), .z2(prandom07_2_z0[4]),
    .z1(prandom07_2_z0[3]), .z0(prandom07_2_z0[2]));
  // NoConnect on prandom07_2_z2
  PRandom07 prandom07_2 (
    .rst(btn0_out), .nxt(and_1_out), .clk(clock_1_out), .z2(prandom07_2_z2), .z1(prandom07_2_z0[1]),
    .z0(prandom07_2_z0[0]));
  Number number_1 (
    .up(risingedge_2_out1), .down(risingedge_3_out1), .rst(btn0_out), .clk(clock_1_out), .numb(LED[4:0]));
  and and_3 (and_3_out, xnor_1_out, sw9);
  or or_1 (or_1_out, and_3_out, and_2_out);
  Multiplexer #(.width(8)) multiplexer_3 (
    .in0({8{1'b0}}), .in1(adder_5_out), .out(multiplexer_3_out), .sel(comparator_1_eq), .en(sw8));
  or or_2 (or_2_out, sw8, sw9);
  and and_4 (and_4_out, risingedge_1_out1, priority_encoder_1_gs);
  Comparator #(.width(5)) comparator_1 (.a(prandom07_2_z0), .b(LED[4:0]), .eq(comparator_1_eq));  // open: gt, lt
  and and_5 (and_5_out, and_4_out, or_2_out);
  Streak streak_1 (.update(and_5_out), .win(or_1_out), .rst(btn0_out), .clk(clock_1_out), .strk(LED[7:5]));
  Chips chips_1 (
    .calc(and_5_out), .even_odd(multiplexer_2_out), .straight_up(multiplexer_3_out), .rst(btn0_out),
    .clk(clock_1_out), .chipsy(chips_1_chipsy));
  // _7_Segment_Display 7_segment_display_1: pin names not known; wires that end beside it: n7_segment_display_1_p1, n7_segment_display_1_p1
  // BCD_to_7_Segment_decoder bcd_to_7_segment_decoder_1: pin names not known; wires that end beside it: LED[7:5]
  // Binairy_to_BCD_converter #(.binvalue(8)) binairy_to_bcd_converter_1: pin names not known; wires that end beside it: chips_1_chipsy
  // _7_Segment_Display 7_segment_display_2: pin names not known; wires that end beside it: n7_segment_display_2_p1, n7_segment_display_2_p1
  // _7_Segment_Display 7_segment_display_3: pin names not known; wires that end beside it: n7_segment_display_3_p1, n7_segment_display_3_p1
  // BCD_to_7_Segment_decoder bcd_to_7_segment_decoder_2: pin names not known
  // BCD_to_7_Segment_decoder bcd_to_7_segment_decoder_3: pin names not known
endmodule

module Number (
  input  up,
  input  down,
  input  rst,
  input  clk,
  output [4:0] numb
);

  wire and_1_out, and_2_out, not_1_out, not_2_out, not_3_out;
  wire [7:5] reg8_1_i;

  not not_1 (not_1_out, up);
  and and_1 (and_1_out, up, not_2_out);
  not not_2 (not_2_out, rst);
  not not_3 (not_3_out, rst);
  and and_2 (and_2_out, not_1_out, down, not_3_out);
  REG8 reg8_1 (
    .I({reg8_1_i, numb}), .CL(rst), .DEC(and_1_out), .INC(and_2_out), .CLK(clk));  // open: Cout, Eout, LD, SL, IL, SR, IR, A
endmodule

module Streak (
  input  update,
  input  win,
  input  rst,
  input  clk,
  output [2:0] strk
);

  wire and_1_out, and_2_out, not_1_out, not_2_out, or_1_out;
  wire [7:3] reg8_1_i;

  not not_1 (not_1_out, win);
  and and_1 (and_1_out, update, win, not_2_out);
  not not_2 (not_2_out, rst);
  or or_1 (or_1_out, rst, and_2_out);
  and and_2 (and_2_out, update, not_1_out);
  REG8 reg8_1 (
    .I({reg8_1_i, strk}), .CL(or_1_out), .SL(and_1_out), .IL(and_1_out), .CLK(clk));  // open: Cout, Eout, LD, SR, IR, DEC, INC, A
endmodule

module Chips (
  input  calc,
  input  [7:0] even_odd,
  input  [7:0] straight_up,
  input  rst,
  input  clk,
  output [7:0] chipsy
);

  wire and_1_out, not_1_out;
  wire [7:0] add8_1_f;

  not not_1 (not_1_out, rst);
  ADD8 add8_1 (.F(add8_1_f), .A(straight_up), .B(even_odd));  // open: C8, C0
  and and_1 (and_1_out, calc, not_1_out);
  REG8 reg8_1 (
    .I(chipsy), .CL(rst), .LD(and_1_out), .CLK(clk), .A(add8_1_f));  // open: Cout, Eout, SL, IL, SR, IR, DEC, INC
endmodule
