// Logisim project RisingEdge-copy.circ as structural Verilog: 1 circuit, main circuit RisingEdge
module RisingEdge (
  input  in1,
  input  clk,
  output out1
);

  wire d_ff_1_qn;

  D_Flip_Flop d_ff_1 (.D(in1), .clk(clk), .Qn(d_ff_1_qn));  // open: Q, preset, reset
  and and_1 (out1, in1, d_ff_1_qn);
endmodule
