// Logisim project dz5-lib.circ as structural Verilog: 5 circuits, main circuit AddrMod
module AddrMod (
  input  rst,
  input  wr,
  input  clk,
  output [3:0] addrWr,
  output [4:0] cnt
);

  wire and_1_out, and_2_out, or_1_out, t_ff_1_q, t_ff_1_qn;

  REG4 reg4_1 (.CL(rst), .INC(wr), .CLK(clk), .I(addrWr));  // open: LD, A, SL, IL, SR, IR, DEC, Cout, Eout
  and and_1 (and_1_out, rst, t_ff_1_q);
  and and_2 (and_2_out, t_ff_1_qn, addrWr[0], addrWr[1], addrWr[2], addrWr[3]);
  T_Flip_Flop t_ff_1 (.T(or_1_out), .clk(clk), .Q(t_ff_1_q), .Qn(t_ff_1_qn));  // open: reset, preset
  or or_1 (or_1_out, and_1_out, and_2_out);
  Multiplexer #(.enable("false"), .width(5)) multiplexer_1 (
    .in0({1'b0, addrWr}), .in1(5'b10000), .out(cnt), .sel(t_ff_1_q));
endmodule

module REG4 (
  input  CL,
  input  LD,
  input  [3:0] A,
  input  SL,
  input  IL,
  input  SR,
  input  IR,
  input  INC,
  input  DEC,
  input  CLK,
  output Cout,
  output Eout,
  output [3:0] I
);

  wire reg1_2_cout, reg1_2_eout, reg1_3_cout, reg1_3_eout, reg1_4_cout, reg1_4_eout;

  REG1 reg1_1 (
    .CL(CL), .LD(LD), .I(A[3]), .SL(SL), .IL(I[2]), .SR(SR), .IR(IR), .CLK(CLK), .A(I[3]), .INC(reg1_2_cout),
    .DEC(reg1_2_eout), .Cout(Cout), .Eout(Eout));
  REG1 reg1_2 (
    .CL(CL), .LD(LD), .I(A[2]), .SL(SL), .IL(I[1]), .SR(SR), .IR(I[3]), .CLK(CLK), .A(I[2]),
    .INC(reg1_3_cout), .DEC(reg1_3_eout), .Cout(reg1_2_cout), .Eout(reg1_2_eout));
  REG1 reg1_3 (
    .CL(CL), .LD(LD), .I(A[1]), .SL(SL), .IL(I[0]), .SR(SR), .IR(I[2]), .CLK(CLK), .A(I[1]),
    .INC(reg1_4_cout), .DEC(reg1_4_eout), .Cout(reg1_3_cout), .Eout(reg1_3_eout));
  REG1 reg1_4 (
    .CL(CL), .LD(LD), .I(A[0]), .SL(SL), .IL(IL), .SR(SR), .IR(I[1]), .CLK(CLK), .A(I[0]), .INC(INC),
    .DEC(DEC), .Cout(reg1_4_cout), .Eout(reg1_4_eout));
endmodule

module MeanGain (
  input  [7:0] gain,
  input  wr,
  input  mean,
  input  rst,
  input  clk,
  input  clAddrRd,
  input  decAddrRd,
  input  S1,
  input  S0,
  input  Cin,
  input  ldL0,
  input  clL0,
  input  ldL1,
  input  clL1,
  input  rdALU,
  input  ldRes,
  input  clRes,
  input  rdS,
  input  rdMem,
  input  rdConst,
  input  rdRes,
  input  ldS,
  input  clS,
  input  srS,
  output [7:0] RES,
  output addrRd0,
  output Cout
);

  wire not_1_out;
  wire [3:0] addrmod_1_addrwr, multiplexer_1_out;
  wire [4:0] addrmod_1_cnt;
  wire [7:0] alu8_1_f, controlled_buffer_1_out, mem16x8_1_dout, reg8_1_i, reg8_2_i, reg8_4_i, reg8_5_i;

  REG8 reg8_1 (
    .CL(clAddrRd), .LD(mean), .A({3'b000, addrmod_1_cnt}), .INC(decAddrRd), .CLK(clk), .I(reg8_1_i));  // open: SL, IL, SR, IR, DEC, Cout, Eout
  AddrMod addrmod_1 (.rst(rst), .wr(wr), .clk(clk), .addrWr(addrmod_1_addrwr), .cnt(addrmod_1_cnt));
  Multiplexer #(.enable("false"), .width(4)) multiplexer_1 (
    .in0(reg8_1_i[3:0]), .in1(addrmod_1_addrwr), .out(multiplexer_1_out), .sel(wr));
  nor nor_1 (addrRd0, reg8_1_i[0], reg8_1_i[1], reg8_1_i[2], reg8_1_i[3], reg8_1_i[4]);
  not not_1 (not_1_out, wr);
  MEM16x8 mem16x8_1 (
    .DIN(gain), .WR_RD(not_1_out), .A3__0(multiplexer_1_out), .CS(1'b1), .CLK(clk), .DOUT(mem16x8_1_dout));
  assign controlled_buffer_1_out = rdMem ? mem16x8_1_dout : 8'bz;  // Controlled_Buffer controlled_buffer_1
  assign controlled_buffer_1_out = rdConst ? 8'hf0 : 8'bz;  // Controlled_Buffer controlled_buffer_2
  REG8 reg8_2 (
    .CL(clL0), .LD(ldL0), .A(controlled_buffer_1_out), .CLK(clk), .I(reg8_2_i));  // open: SL, IL, SR, IR, DEC, INC, Cout, Eout
  REG8 reg8_3 (
    .CL(clRes), .LD(ldRes), .A(controlled_buffer_1_out), .CLK(clk), .I(RES));  // open: SL, IL, SR, IR, DEC, INC, Cout, Eout
  assign controlled_buffer_1_out = rdRes ? RES : 8'bz;  // Controlled_Buffer controlled_buffer_3
  REG8 reg8_4 (
    .CL(clL1), .LD(ldL1), .A(controlled_buffer_1_out), .CLK(clk), .I(reg8_4_i));  // open: SL, IL, SR, IR, DEC, INC, Cout, Eout
  ALU8 alu8_1 (.A(reg8_2_i), .B(reg8_4_i), .Cin(Cin), .S0(S0), .S1(S1), .Cout(Cout), .F(alu8_1_f));
  assign controlled_buffer_1_out = rdALU ? alu8_1_f : 8'bz;  // Controlled_Buffer controlled_buffer_4
  REG8 reg8_5 (
    .CL(clS), .LD(ldS), .A(alu8_1_f), .SR(srS), .CLK(clk), .I(reg8_5_i));  // open: SL, IL, IR, DEC, INC, Cout, Eout
  assign controlled_buffer_1_out = rdS ? reg8_5_i : 8'bz;  // Controlled_Buffer controlled_buffer_5
endmodule

module ALU8 (
  input  [7:0] A,
  input  [7:0] B,
  input  Cin,
  input  S0,
  input  S1,
  output Cout,
  output [7:0] F
);

  wire adder_1_cout, adder_2_cout, subtractor_1_bout, undriven;
  wire [7:0] adder_1_out, adder_2_out, and_1_out, subtractor_1_out;

  Subtractor subtractor_1 (.a(A), .b(B), .out(subtractor_1_out), .bin(undriven), .bout(subtractor_1_bout));
  Adder adder_1 (.a(A), .b(B), .out(adder_1_out), .cout(adder_1_cout));  // open: cin
  Multiplexer #(.enable("false"), .select(2), .width(8)) multiplexer_1 (
    .in0(subtractor_1_out), .in1(adder_1_out), .in2(adder_2_out), .in3(and_1_out), .out(F), .sel({S1, S0}));
  Adder adder_2 (.a(A), .b({8{1'b0}}), .out(adder_2_out), .cin(Cin), .cout(adder_2_cout));
  Multiplexer #(.enable("false"), .select(2)) multiplexer_2 (
    .in0(subtractor_1_bout), .in1(adder_1_cout), .in2(adder_2_cout), .in3(1'b0), .out(Cout), .sel({S1, S0}));
  assign and_1_out = B & A;  // AND_Gate and_1, 8 bits wide
endmodule

module FallingEdge (
  input  in1,
  input  clk,
  output out1
);

  wire d_ff_1_q, not_1_out;

  not not_1 (not_1_out, in1);
  D_Flip_Flop d_ff_1 (.D(in1), .clk(clk), .Q(d_ff_1_q));  // open: Qn, preset, reset
  and and_1 (out1, not_1_out, d_ff_1_q);
endmodule
