// Logisim project dz5.circ as structural Verilog: 4 circuits, main circuit dz5
module dz5 (
  input  SW0,
  input  SW1,
  input  SW2,
  input  SW3,
  input  SW4,
  input  SW5,
  input  SW6,
  input  SW7,
  input  SW8,
  input  SW9,
  output [7:0] out_11
);

  wire and_1_out, and_2_out, and_3_out, and_4_out, BTN0_out, BTN1_out, BTN2_out, CLK_out, comparator_1_eq,
       comparator_2_lt, fallingedge_1_out1, not_1_out, or_1_out, prandom07_2_z2, priority_encoder_1_gs,
       risingedge_1_out1, t_ff_1_qn, timer_1_out1, xnor_1_out;
  wire [1:0] priority_encoder_1_out;
  wire [2:0] undriven;
  wire [4:0] number_1_numb, prandom07_1_z0;
  wire [7:0] adder_1_out, adder_2_out, adder_3_out, adder_4_out, adder_5_out, chips1_1_chipsy, chips1_1_gain,
       meangainctrl_1_out_6, multiplexer_1_out, multiplexer_2_out, multiplexer_3_out, multiplexer_4_out,
       multiplexer_5_out;

  Button BTN0 (.out(BTN0_out));
  Button BTN1 (.out(BTN1_out));
  Clock CLK (.out(CLK_out));
  Button BTN2 (.out(BTN2_out));
  T_Flip_Flop t_ff_1 (.T(and_1_out), .clk(CLK_out), .Qn(t_ff_1_qn), .reset(BTN0_out));  // open: Q, preset
  and and_1 (and_1_out, BTN1_out, t_ff_1_qn);
  xnor xnor_1 (xnor_1_out, prandom07_1_z0[3], SW3);
  Priority_Encoder #(.select(2)) priority_encoder_1 (
    .in0(SW4), .in1(SW5), .in2(SW6), .in3(SW7), .out(priority_encoder_1_out), .gs(priority_encoder_1_gs));  // open: en_out, en_in
  Multiplexer #(.select(2), .width(8)) multiplexer_1 (
    .in0(8'h1), .in1(8'h2), .in2(8'h4), .in3(8'h6), .out(multiplexer_1_out), .sel(priority_encoder_1_out),
    .en(priority_encoder_1_gs));
  and and_2 (and_2_out, BTN1_out, t_ff_1_qn);
  Multiplexer #(.width(8)) multiplexer_2 (
    .in0({8{1'b0}}), .in1(adder_1_out), .out(multiplexer_2_out), .sel(xnor_1_out), .en(SW8));
  Adder adder_1 (.a(multiplexer_1_out), .b(multiplexer_1_out), .out(adder_1_out));  // open: cin, cout
  Timer timer_1 (.start(BTN1_out), .rst(BTN0_out), .clk(CLK_out), .out1(timer_1_out1));
  FallingEdge fallingedge_1 (.out1(fallingedge_1_out1), .in1(timer_1_out1), .clk(CLK_out));
  RisingEdge risingedge_1 (.in1(BTN2_out), .clk(CLK_out), .out1(risingedge_1_out1));
  Number number_1 (.up(SW0), .down(SW1), .rst(BTN0_out), .clk(CLK_out), .numb(number_1_numb));
  Adder adder_2 (.a(adder_1_out), .b(adder_1_out), .out(adder_2_out));  // open: cin, cout
  and and_3 (and_3_out, timer_1_out1, ~prandom07_1_z0[2], ~prandom07_1_z0[1], prandom07_1_z0[0]);  // AND_Gate
  Adder adder_3 (.a(adder_2_out), .b(adder_2_out), .out(adder_3_out));  // open: cin, cout
  Adder adder_4 (.a(adder_3_out), .b(adder_3_out), .out(adder_4_out));  // open: cin, cout
  PRandom07 prandom07_1 (
    .rst(BTN0_out), .nxt(timer_1_out1), .clk(CLK_out), .z2(prandom07_1_z0[2]), .z1(prandom07_1_z0[1]),
    .z0(prandom07_1_z0[0]));
  // NoConnect on prandom07_2_z2
  PRandom07 prandom07_2 (
    .rst(BTN0_out), .nxt(and_3_out), .clk(CLK_out), .z2(prandom07_2_z2), .z1(prandom07_1_z0[4]),
    .z0(prandom07_1_z0[3]));
  Multiplexer #(.width(8)) multiplexer_3 (
    .in0({8{1'b0}}), .in1(adder_5_out), .out(multiplexer_3_out), .sel(comparator_1_eq), .en(SW9));
  Adder adder_5 (.a(adder_4_out), .b(adder_4_out), .out(adder_5_out));  // open: cin, cout
  Comparator #(.mode("unsigned"), .width(5)) comparator_1 (
    .a(prandom07_1_z0), .b(number_1_numb), .eq(comparator_1_eq));  // open: gt, lt
  Multiplexer #(.enable("false"), .width(8)) multiplexer_4 (
    .in0({8{1'b0}}), .in1(multiplexer_2_out), .out(multiplexer_4_out), .sel(not_1_out));
  Multiplexer #(.enable("false"), .width(8)) multiplexer_5 (
    .in0({8{1'b0}}), .in1(multiplexer_3_out), .out(multiplexer_5_out), .sel(not_1_out));
  or or_1 (or_1_out, SW8, SW9);
  and and_4 (and_4_out, fallingedge_1_out1, priority_encoder_1_gs, not_1_out, or_1_out);
  MeanGainCtrl meangainctrl_1 (
    .gain(chips1_1_gain), .wr(and_4_out), .mean(risingedge_1_out1), .rst(BTN0_out), .clk(CLK_out),
    .out_6(meangainctrl_1_out_6));
  Comparator comparator_2 (.a(chips1_1_chipsy), .b(multiplexer_1_out), .lt(comparator_2_lt));  // open: gt, eq
  Chips1 chips1_1 (
    .init(and_2_out), .calc(fallingedge_1_out1), .stake(multiplexer_1_out), .even_odd(multiplexer_4_out),
    .straight_up(multiplexer_5_out), .rst(BTN0_out), .clk(CLK_out), .gain(chips1_1_gain),
    .chipsy(chips1_1_chipsy));
  Multiplexer #(.enable("false"), .width(8)) multiplexer_6 (
    .in0({undriven, number_1_numb}), .in1(meangainctrl_1_out_6), .out(out_11), .sel(SW2));
  _7_Segment_Display u_7_segment_display_1 ();  // open: g, f, a, b, e, d, c, dp
  // BCD_to_7_Segment_decoder bcd_to_7_segment_decoder_1: pin names not known
  not not_1 (not_1_out, comparator_2_lt);
  // Binairy_to_BCD_converter #(.binvalue(8)) binairy_to_bcd_converter_1: pin names not known; wires that end beside it: chips1_1_chipsy
  _7_Segment_Display u_7_segment_display_2 ();  // open: g, f, a, b, e, d, c, dp
  // BCD_to_7_Segment_decoder bcd_to_7_segment_decoder_2: pin names not known
  _7_Segment_Display u_7_segment_display_3 ();  // open: g, f, a, b, e, d, c, dp
  // BCD_to_7_Segment_decoder bcd_to_7_segment_decoder_3: pin names not known
endmodule

module Chips1 (
  input  init,
  input  calc,
  input  [7:0] stake,
  input  [7:0] even_odd,
  input  [7:0] straight_up,
  input  rst,
  input  clk,
  output [7:0] gain,
  output [7:0] chipsy
);

  wire and_1_out, or_1_out;
  wire [7:0] adder_2_out, multiplexer_1_out, subtractor_1_out;

  or or_1 (or_1_out, init, calc);
  and and_1 (and_1_out, or_1_out, ~rst);  // AND_Gate
  REG8 reg8_1 (
    .I(chipsy), .CL(rst), .LD(and_1_out), .CLK(clk), .A(multiplexer_1_out));  // open: Cout, Eout, SL, IL, SR, IR, DEC, INC
  Adder adder_1 (.a(even_odd), .b(straight_up), .out(gain));  // open: cin, cout
  Subtractor subtractor_1 (.a(chipsy), .b(stake), .out(subtractor_1_out));  // open: bin, bout
  Multiplexer #(.enable("false"), .width(8)) multiplexer_1 (
    .in0(adder_2_out), .in1(8'h64), .out(multiplexer_1_out), .sel(init));
  Adder adder_2 (.a(gain), .b(subtractor_1_out), .out(adder_2_out));  // open: cin, cout
endmodule

module Timer (
  input  start,
  input  rst,
  input  clk,
  output out1
);

  wire and_1_out, d_ff_1_q, risingedge_1_out1;
  wire [2:0] prandom07_1_z2;
  wire [7:0] reg8_1_i;

  RisingEdge risingedge_1 (.in1(start), .clk(clk), .out1(risingedge_1_out1));
  PRandom07 prandom07_1 (
    .rst(rst), .nxt(risingedge_1_out1), .clk(clk), .z2(prandom07_1_z2[0]), .z1(prandom07_1_z2[1]),
    .z0(prandom07_1_z2[2]));
  REG8 reg8_1 (
    .I(reg8_1_i), .CL(rst), .LD(and_1_out), .INC(out1), .CLK(clk), .A({{5{1'b0}}, prandom07_1_z2}));  // open: Cout, Eout, SL, IL, SR, IR, DEC
  D_Flip_Flop d_ff_1 (.D(risingedge_1_out1), .clk(clk), .Q(d_ff_1_q));  // open: Qn, preset, reset
  and and_1 (and_1_out, ~rst, d_ff_1_q, ~out1);  // AND_Gate
  or or_1 (out1, reg8_1_i[2], reg8_1_i[1], reg8_1_i[0]);
endmodule

module MeanGainCtrl (
  input  [7:0] gain,
  input  wr,
  input  mean,
  input  rst,
  input  clk,
  output [7:0] out_6
);

  wire and_1_out, and_2_out, and_3_out, and_4_out, and_5_out, meangain_1_addrrd0, meangain_1_cout, or_1_out,
       or_2_out, or_3_out, or_4_out, or_5_out, or_6_out, T0_out, T1_out, T2_out, T3_out, T4_out, T5_out,
       T6_out, T7_out, t_ff_1_q, t_ff_1_qn, t_ff_2_q, t_ff_2_qn, t_ff_3_q, t_ff_3_qn;

  or or_1 (or_1_out, T2_out, T4_out, T5_out, T6_out);
  or or_2 (or_2_out, T3_out, T4_out, T5_out, T6_out);
  or or_3 (or_3_out, T3_out, T5_out, T6_out);
  MeanGain meangain_1 (
    .gain(gain), .wr(wr), .mean(mean), .rst(rst), .clk(clk), .clAddrRd(1'b0), .decAddrRd(T1_out), .S1(1'b0),
    .S0(1'b1), .Cin(1'b0), .ldL0(or_1_out), .clL0(T0_out), .ldL1(or_2_out), .clL1(T0_out), .rdALU(or_3_out),
    .ldRes(T7_out), .clRes(1'b0), .rdS(T7_out), .rdMem(T2_out), .rdConst(T4_out), .rdRes(1'b0), .ldS(T3_out),
    .clS(T0_out), .srS(T6_out), .RES(out_6), .addrRd0(meangain_1_addrrd0), .Cout(meangain_1_cout));
  and and_1 (and_1_out, T0_out, mean, ~meangain_1_addrrd0);  // AND_Gate
  and and_2 (and_2_out, T3_out, ~meangain_1_addrrd0);  // AND_Gate
  and and_3 (and_3_out, T0_out, mean, meangain_1_addrrd0);
  and and_4 (and_4_out, T3_out, meangain_1_addrrd0);
  and and_5 (and_5_out, T6_out, ~meangain_1_cout);  // AND_Gate
  T_Flip_Flop t_ff_1 (.T(or_4_out), .clk(clk), .Q(t_ff_1_q), .Qn(t_ff_1_qn), .reset(rst));  // open: preset
  or or_4 (or_4_out, T2_out, T3_out, T4_out, T7_out);
  T_Flip_Flop t_ff_2 (.T(or_5_out), .clk(clk), .Q(t_ff_2_q), .Qn(t_ff_2_qn), .reset(rst));  // open: preset
  or or_5 (or_5_out, and_1_out, T1_out, and_2_out, T5_out);
  T_Flip_Flop t_ff_3 (.T(or_6_out), .clk(clk), .Q(t_ff_3_q), .Qn(t_ff_3_qn), .reset(rst));  // open: preset
  or or_6 (or_6_out, and_3_out, and_4_out, T7_out, and_5_out);
  and T0 (T0_out, t_ff_1_qn, t_ff_2_qn, t_ff_3_qn);
  and T1 (T1_out, t_ff_1_qn, t_ff_2_qn, t_ff_3_q);
  and T2 (T2_out, t_ff_1_qn, t_ff_2_q, t_ff_3_q);
  and T3 (T3_out, t_ff_1_q, t_ff_2_q, t_ff_3_q);
  and T5 (T5_out, t_ff_1_q, t_ff_2_q, t_ff_3_qn);
  and T4 (T4_out, t_ff_1_qn, t_ff_2_q, t_ff_3_qn);
  and T6 (T6_out, t_ff_1_q, t_ff_2_qn, t_ff_3_qn);
  and T7 (T7_out, t_ff_1_q, t_ff_2_qn, t_ff_3_q);
endmodule
